# Fritzing sketch AnalogInput (saved by Fritzing 0.1.b)
breadboards: 1

parts:
  Part1 = Arduino Diecimila (deprecated) [package=THT]
  LED1 = Red LED - 5mm
  R1 = Trimmer Potentiometer [package=THT]

nets:
  N1: Part1.GND, Part1.ground, LED1.cathode, R1.leg2
  N2: Part1.D13, LED1.anode
  N3: Part1.+5V, R1.leg1
  N4: Part1.A2, R1.wiper
