# Fritzing sketch AnalogInputFSR (saved by Fritzing 0.2.2)
breadboards: 1

parts:
  Arduino1 = Arduino Diecimila (deprecated) [package=THT]
  LED1 = Red LED - 5mm
  J1 = Basic Force Sensing Resistor (FSR) [package=THT]
  R1 = 10k Ω Resistor [package=THT]

nets:
  N1: Arduino1.GND, LED1.cathode, R1.Pin_0
  N2: Arduino1.D13, LED1.anode
  N3: Arduino1.+5V, J1.pin_0
  N4: Arduino1.A2, J1.pin_1, R1.Pin_1

notes:
  In this example, FSR values are read in through an 'Analog In' pin. The values are then used to control the blinking rate of an LED.
  Related example: http://arduino.cc/en/Tutorial/AnalogInput
