# Fritzing sketch AnalogInputPot (saved by Fritzing 0.2.2)
breadboards: 1

parts:
  Arduino1 = Arduino Diecimila (deprecated) [package=THT]
  LED1 = Red LED - 5mm
  R1 = Rotary Potentiometer (Large) [package=THT]

nets:
  N1: Arduino1.GND, LED1.cathode, R1.leg2
  N2: Arduino1.D13, LED1.anode
  N3: Arduino1.+5V, R1.leg1
  N4: Arduino1.A3, R1.wiper

notes:
  In this example, potentiometer values are read in through an 'Analog In' pin. The values are then used to control the blinking rate of an LED.
  Related example: http://arduino.cc/en/Tutorial/AnalogInput
