# Fritzing sketch AnalogInputThermistor (saved by Fritzing 0.2.2)
breadboards: 1

parts:
  Arduino1 = Arduino Diecimila (deprecated) [package=THT]
  R1 = Temperature Sensor (Thermistor) [package=THT]
  R2 = 1k Ω Resistor [package=THT]
  LED1 = Blue LED - 5mm

nets:
  N1: Arduino1.GND, R2.Pin_0, LED1.cathode
  N2: Arduino1.D13, LED1.anode
  N3: Arduino1.+5V, R1.pin_0
  N4: Arduino1.A2, R1.pin_1, R2.Pin_1

notes:
  In this example, thermistor values are read in through an 'Analog In' pin. The values are then used to control the blinking rate of an LED.
  Related example: http://arduino.cc/en/Tutorial/AnalogInput
