# Fritzing sketch AnalogInputToServo (saved by Fritzing 0.1.b)
breadboards: 1

parts:
  Part1 = Arduino Diecimila (deprecated) [package=THT]
  R1 = Trimmer Potentiometer [package=THT]
  J1 = Basic Servo
  J1_2 = Basic Servo
  J1_3 = Basic Servo

nets:
  GND: Part1.D2, Part1.GND, Part1.ground, R1.leg2, J1.gnd, J1.pulse, J1_2.gnd, J1_2.pulse, J1_3.gnd, J1_3.pulse
  VCC: Part1.+5V, R1.leg1, J1.vcc, J1_2.vcc, J1_3.vcc
  N1: Part1.A2, R1.wiper
