# Fritzing sketch Blink (saved by Fritzing 0.2.2)

parts:
  Arduino1 = Arduino Diecimila (deprecated) [package=THT]
  LED1 = Red LED - 5mm

nets:
  N1: Arduino1.GND, LED1.cathode
  N2: Arduino1.D13, LED1.anode

notes:
  In this very simple example, Arduino will be programmed to blink the LED on pin 13.
  Related example:
  http://arduino.cc/en/Tutorial/Blink
