# Fritzing sketch Loop (saved by Fritzing 0.2.2)
breadboards: 1

parts:
  Arduino1 = Arduino Diecimila (deprecated) [package=THT]
  LED1 = Red LED - 5mm
  R1 = 220 Ω Resistor [package=THT]
  LED2 = Red LED - 5mm
  R2 = 220 Ω Resistor [package=THT]
  LED3 = Red LED - 5mm
  R3 = 220 Ω Resistor [package=THT]
  LED4 = Red LED - 5mm
  R4 = 220 Ω Resistor [package=THT]
  LED5 = Red LED - 5mm
  R5 = 220 Ω Resistor [package=THT]
  LED6 = Red LED - 5mm
  R6 = 220 Ω Resistor [package=THT]

nets:
  N1: Arduino1.GND, LED1.cathode, LED2.cathode, LED3.cathode, LED4.cathode, LED5.cathode, LED6.cathode
  N2: Arduino1.D7, R1.Pin_1
  N3: Arduino1.D6, R2.Pin_1
  N4: Arduino1.D5, R3.Pin_1
  N5: Arduino1.D4, R4.Pin_1
  N6: Arduino1.D3, R5.Pin_1
  N7: Arduino1.D2, R6.Pin_1
  N8: LED1.anode, R1.Pin_0
  N9: LED2.anode, R2.Pin_0
  N10: LED3.anode, R3.Pin_0
  N11: LED4.anode, R4.Pin_0
  N12: LED5.anode, R5.Pin_0
  N13: LED6.anode, R6.Pin_0

notes:
  In this example, six leds are controlled by digital out pins.
  Related Example:
  http://arduino.cc/en/Tutorial/Loop
