# Fritzing sketch TrafficLight (saved by Fritzing 0.1.b)
breadboards: 1

parts:
  Arduino1 = Arduino Diecimila (deprecated) [package=THT]
  LED1 = Red LED - 5mm
  Part1 = 220 Ω Resistor [package=THT]
  LED2 = yellow LED - 5mm
  Part2 = 220 Ω Resistor [package=THT]
  LED3 = green LED - 5mm
  Part3 = 220 Ω Resistor [package=THT]
  S1 = Pushbutton [package=THT]
  Part4 = 220 Ω Resistor [package=THT]
  LED4 = Red LED - 5mm
  Part5 = 220 Ω Resistor [package=THT]
  LED5 = green LED - 5mm
  Part6 = 220 Ω Resistor [package=THT]

nets:
  N1: Arduino1.GND, LED1.cathode, LED2.cathode, LED3.cathode, Part4.Pin_0, LED4.cathode, LED5.cathode
  N2: Arduino1.D12, Part1.Pin_1
  N3: Arduino1.D11, Part2.Pin_1
  N4: Arduino1.D10, Part3.Pin_1
  N5: Arduino1.D9, Part5.Pin_1
  N6: Arduino1.D8, Part6.Pin_1
  N7: Arduino1.D2, S1.leg1, Part4.Pin_1
  N8: Arduino1.+5V, S1.leg0
  N9: LED1.anode, Part1.Pin_0
  N10: LED2.anode, Part2.Pin_0
  N11: LED3.anode, Part3.Pin_0
  N12: LED4.anode, Part5.Pin_0
  N13: LED5.anode, Part6.Pin_0
