# Fritzing sketch npnPowerTransistor (saved by Fritzing 0.2.2)
breadboards: 1

parts:
  Arduino1 = Arduino Diecimila (deprecated) [package=THT]
  Q1 = npn-Powertransistor [package="TO220 [THT]"]
  R1 = 1k Ω Resistor [package=THT]
  LED1 = Red LED - 5mm
  R2 = 220 Ω Resistor [package=THT]
  LED2 = Red LED - 5mm
  R3 = 220 Ω Resistor [package=THT]
  LED3 = Red LED - 5mm
  R4 = 220 Ω Resistor [package=THT]
  LED4 = Red LED - 5mm
  R5 = 220 Ω Resistor [package=THT]

nets:
  N1: Arduino1.GND, Q1.emitter
  N2: Arduino1.D9, R1.Pin_0
  N3: Arduino1.+5V, R2.Pin_1, R3.Pin_1, R4.Pin_1, R5.Pin_1
  N4: Q1.base, R1.Pin_1
  N5: Q1.collector, LED1.cathode, LED2.cathode, LED3.cathode, LED4.cathode
  N6: LED1.anode, R2.Pin_0
  N7: LED2.anode, R3.Pin_0
  N8: LED3.anode, R4.Pin_0
  N9: LED4.anode, R5.Pin_0

notes:
  Using a power transistor with an Arduino pinout will allow you to control outputs with a higher current or voltage source that Arduino pins support.
  Related example:
  http://itp.nyu.edu/physcomp/Tutorials/HighCurrentLoads
