# Fritzing sketch traffic_light (saved by Fritzing 0.1.b)
breadboards: 1

parts:
  Arduino1 = Arduino Diecimila (deprecated) [package=THT]
  LED1 = Red LED - 5mm
  R1 = basic-resistor-220
  LED2 = yellow LED - 5mm
  R2 = basic-resistor-220
  LED3 = green LED - 5mm
  R3 = basic-resistor-220
  S1 = Pushbutton [package=THT]
  R4 = basic-resistor-1k
  LED4 = Red LED - 5mm
  R5 = basic-resistor-220
  LED5 = green LED - 5mm
  R6 = basic-resistor-220

nets:
  N1: Arduino1.GND, LED1.cathode, LED2.cathode, LED3.cathode, R4.connector0, LED4.cathode, LED5.cathode
  N2: Arduino1.D13, R1.connector1
  N3: Arduino1.D12, R2.connector1
  N4: Arduino1.D11, R3.connector1
  N5: Arduino1.D4, S1.leg1, R4.connector1
  N6: Arduino1.D3, R5.connector1
  N7: Arduino1.D2, R6.connector1
  N8: Arduino1.+5V, S1.leg0
  N9: LED1.anode, R1.connector0
  N10: LED2.anode, R2.connector0
  N11: LED3.anode, R3.connector0
  N12: LED4.anode, R5.connector0
  N13: LED5.anode, R6.connector0
