# Fritzing sketch 555TouchSwitch (saved by Fritzing 0.2.2)
breadboards: 1

parts:
  Arduino1 = Arduino Diecimila (deprecated) [package=THT]
  U1 = 555 Timer [package="DIP8 [THT]"]
  R1 = 100k Ω Resistor [package=THT]
  C2 = Ceramic Capacitor [package=THT]
  C5 = Electrolytic Capacitor [package=THT]

nets:
  N1: Arduino1.GND, U1.Ground, C2.pin_0, C5.-
  N2: Arduino1.D6, U1.Output
  N3: Arduino1.+5V, U1.Reset, U1.Vcc_Supply_Voltage, R1.Pin_0
  N4: U1.Control_Voltage, C2.pin_1
  N5: U1.Threshold, U1.Discharge, R1.Pin_1, C5.+

notes:
  This is a 555 timer touch switch circuit based on a Forrest Mim's circuit. The yellow wire serves as the touch sensor. Pin 3 on the 555 timer is the output pin and is read by Arduino's Pin 6.
