# Fritzing sketch Arduino-no-FTDI (saved by Fritzing 0.2.2)
breadboards: 1

parts:
  C1 = Electrolytic Capacitor [package=THT]
  C2 = Electrolytic Capacitor [package=THT]
  U1 = Voltage Regulator - 5V [package="TO220 [THT]"]
  U2 = atmega168 [package="DIP28 [THT]"]
  R1 = 1k Ω Resistor [package=THT]
  S1 = Pushbutton [package=THT]
  C3 = Ceramic Disk Capacitor [package=THT]
  C4 = Ceramic Disk Capacitor [package=THT]
  XTAL1 = Crystal [package=THT]
  VCC1 = obsolete Battery

nets:
  N1: C1.-, C2.-, U1.GND, U2.Pin_8, U2.Pin_22, S1.Pin_3, S1.Pin_4, C3.pin_1, C4.pin_0, VCC1.-
  N2: C1.+, U1.input_voltage, VCC1.+
  N3: C2.+, U1.output_voltage, U2.Pin_7, U2.Pin_20, U2.Pin_21, R1.Pin_0
  N4: U2.Pin_1, R1.Pin_1, S1.Pin_1, S1.Pin_2
  N5: U2.Pin_9, C4.pin_1, XTAL1.pin_0
  N6: U2.Pin_10, C3.pin_0, XTAL1.pin_1

notes:
  This is a breadboarded Arduino without an FTDI chip.
  *You could program the chip with a USB-Serial breakout board or
  *You could program the chip with an Arduino board and then pop it in the circuit.
  The power source should be at least 7 volts (we don't have that part yet).
  Related example:
  http://itp.nyu.edu/physcomp/Tutorials/ArduinoBreadboard
