# Fritzing sketch DC_motor_control (saved by Fritzing 0.1.14)
breadboards: 1

parts:
  IC1 = H-Bridge [package=THT]
  Arduino1 = Arduino Diecimila (deprecated) [package=THT]
  M1 = DC Motor
  S1 = Pushbutton [package=THT]
  R1 = 1k Ω Resistor [package=THT]

nets:
  N1: IC1.1_2EN, Arduino1.D4
  N2: IC1.1A, Arduino1.D5
  N3: IC1.1Y, M1.pin_1
  GND1: IC1.GND1, IC1.GND2, IC1.GND3, IC1.GND4, Arduino1.GND, R1.Pin_0
  N4: IC1.2Y, M1.pin_2
  N5: IC1.2A, Arduino1.D12
  N6: IC1.VCC2, Arduino1.3V3
  N7: Arduino1.D2, S1.leg1, R1.Pin_1
  N8: Arduino1.+5V, S1.leg0
