# Fritzing sketch VoltageRegulator_7800series (saved by Fritzing 0.11.b)
breadboards: 1

parts:
  C1 = Electrolytic Capacitor [package=THT]
  C2 = Electrolytic Capacitor [package=THT]
  U1 = Voltage Regulator - 5V [package="TO220 [THT]"]

nets:
  N1: C1.-, C2.-, U1.GND
  N2: C1.+, U1.input_voltage
  N3: C2.+, U1.output_voltage
