# Fritzing sketch VoltageRegulator_with_switch (saved by Fritzing 0.2.2)
breadboards: 1

parts:
  S1 = Toggle Switch [package=THT]
  C1 = Electrolytic Capacitor [package=THT]
  C2 = Electrolytic Capacitor [package=THT]
  U1 = Voltage Regulator - 5V [package="TO220 [THT]"]
  VCC1 = obsolete Battery

nets:
  N1: S1.COM, VCC1.+
  N2: S1.L2, C1.+, U1.input_voltage
  N3: C1.-, C2.-, U1.GND, VCC1.-
  N4: C2.+, U1.output_voltage

notes:
  This example uses a 7805 voltage regulator to regulate voltage to 5volts. There is a switch to turn power to the circuit on and off. The battery should be at least 7v (we don't have the part yet).
