# Fritzing sketch 555TouchSwitch (saved by Fritzing 0.5.0b)
breadboards: 1

parts:
  U1 = 555 Timer [package="DIP8 [THT]"]
  Arduino2 = Arduino
  ANT1 = Antenna
  R2 = Resistor [resistance=100k package=THT]
  C6 = Ceramic Capacitor [capacitance=100nF rated_voltage=35V package="200 mil [THT, multilayer]"]
  C5 = Electrolytic Capacitor [capacitance=100nF rated_voltage=35V package="100 mil [THT, electrolytic]"]

nets:
  N1: U1.Ground, Arduino2.GND, C6.0, C5.-
  N2: U1.Trigger, ANT1.antenna_lead
  N3: U1.Output, Arduino2.D6
  N4: U1.Reset, U1.Vcc_Supply_Voltage, Arduino2.+5V, R2.Pin_0
  N5: U1.Control_Voltage, C6.1
  N6: U1.Threshold, U1.Discharge, R2.Pin_1, C5.+

notes:
  This is a 555 timer touch switch circuit based on a Forrest Mims circuit. The yellow wire serves as the touch sensor. Pin 3 on the 555 timer is the output signal and is read by Pin 6 on the Arduino.
  http://talkingelectronics.com/projects/TouchSwitch/TouchSwitch-1.html
