# Fritzing sketch 555TouchSwitch (saved by Fritzing 0.7.0b)
breadboards: 1

parts:
  U1 = 555 Timer [package="DIP8 [THT]"]
  TouchSwitch = Antenna
  R1 = Resistor [resistance=100k tolerance=±5% package=THT]
  C2 = Ceramic Capacitor [capacitance=100nF rated_voltage=35V package="200 mil [THT, multilayer]"]
  C1 = Ceramic Capacitor [capacitance=100nF rated_voltage=35V package="200 mil [THT, multilayer]"]
  Arduino2 = Arduino

nets:
  GND: U1.Ground, C2.0, C1.1, Arduino2.GND
  N1: U1.Trigger, TouchSwitch.antenna_lead
  N2: U1.Output, Arduino2.D6
  N3: U1.Reset, U1.Vcc_Supply_Voltage, R1.Pin_0, Arduino2.+5V
  N4: U1.Control_Voltage, C2.1
  N5: U1.Threshold, U1.Discharge, R1.Pin_1, C1.0

notes:
  This is a 555 timer touch switch circuit based on a Forrest Mims circuit. The yellow wire serves as the touch sensor. Pin 3 on the 555 timer is the output signal and is read by Pin 6 on the Arduino.
  http://talkingelectronics.com/projects/TouchSwitch/TouchSwitch-1.html

// code stored in the sketch: ___lockfile___.txt

