# Fritzing sketch AnalogInputFSR (saved by Fritzing 0.3.9b)
breadboards: 1

parts:
  LED1 = Red LED - 5mm
  J1 = Basic Force Sensing Resistor (FSR) [package=THT]
  Arduino2 = Arduino
  R2 = Resistor [resistance=10k package=THT]

nets:
  N1: LED1.cathode, Arduino2.GND, R2.Pin_0
  N2: LED1.anode, Arduino2.D13
  N3: J1.pin_0, Arduino2.+5V
  N4: J1.pin_1, Arduino2.A2, R2.Pin_1

notes:
  In this example, FSR values are read in through an 'Analog In' pin. The values are then used to control the blinking rate of an LED.
  Related examples: http://www.ladyada.net/learn/sensors/fsr.html
  http://itp.nyu.edu/physcomp/sensors/Reports/ForceSensorResistor
  Related code: http://arduino.cc/en/Tutorial/AnalogInput
