# Fritzing sketch AnalogInputFSR (saved by Fritzing 0.7.0b)
breadboards: 1

parts:
  J1 = Basic Force Sensing Resistor (FSR) [package=THT]
  R2 = Resistor [resistance=10k tolerance=±5% package=THT]
  LED2 = LED - 5mm [color="Red (633nm)" package="5 mm [THT]"]
  Arduino2 = Arduino

nets:
  N1: J1.pin_0, Arduino2.+5V
  N2: J1.pin_1, R2.Pin_1, Arduino2.A2
  N3: R2.Pin_0, LED2.cathode, Arduino2.GND
  N4: LED2.anode, Arduino2.D13

notes:
  In this example, FSR values are read in through an 'Analog In' pin. The values are then used to control the blinking rate of an LED.
  Related examples: http://www.ladyada.net/learn/sensors/fsr.html
  http://itp.nyu.edu/physcomp/sensors/Reports/ForceSensorResistor
  Related code: http://arduino.cc/en/Tutorial/AnalogInput

// code stored in the sketch: ___lockfile___.txt

