# Fritzing sketch AnalogInputOutput (saved by Fritzing 0.3.9b)
breadboards: 1

parts:
  LED1 = Red LED - 5mm
  R3 = Rotary Potentiometer (Large) [package=THT]
  Arduino2 = Arduino
  R4 = Resistor [resistance=220 package=THT]

nets:
  N1: LED1.cathode, R3.leg2, Arduino2.GND
  N2: LED1.anode, R4.Pin_0
  N3: R3.leg1, Arduino2.+5V
  N4: R3.wiper, Arduino2.A3
  N5: Arduino2.D3, R4.Pin_1

notes:
  In this example, potentiometer values are read in through an 'Analog In' pin. The values are then used to control the modulation of an LED on a PWM pin. Related examples: http://arduino.cc/en/Tutorial/AnalogInput http://arduino.cc/en/Tutorial/Fading
