# Fritzing sketch AnalogInputOutput (saved by Fritzing 0.7.0b)
breadboards: 1

parts:
  R4 = Resistor [resistance=220 tolerance=±5% package=THT]
  R3 = Rotary Potentiometer (Large) [maximum_resistance=100kΩ package=THT]
  LED2 = LED - 5mm [color="Red (633nm)" package="5 mm [THT]"]
  Arduino2 = Arduino

nets:
  N1: R4.Pin_0, LED2.anode
  N2: R4.Pin_1, Arduino2.D3
  N3: R3.leg1, Arduino2.+5V
  N4: R3.wiper, Arduino2.A3
  N5: R3.leg2, LED2.cathode, Arduino2.GND

notes:
  In this example, potentiometer values are read in through an 'Analog In' pin. The values are then used to control the modulation of an LED on a PWM pin. Related examples: http://arduino.cc/en/Tutorial/AnalogInput http://arduino.cc/en/Tutorial/Fading

// code stored in the sketch: ___lockfile___.txt

