# Fritzing sketch AnalogInputPot (saved by Fritzing 0.3.15b)
breadboards: 1

parts:
  R1 = Rotary Potentiometer (Large) [package=THT]
  Arduino2 = Arduino
  LED2 = Red LED - 5mm

nets:
  N1: R1.leg1, Arduino2.+5V
  N2: R1.wiper, Arduino2.A3
  N3: R1.leg2, Arduino2.GND, LED2.cathode
  N4: Arduino2.D13, LED2.anode

notes:
  In this example, potentiometer values are read in through an 'Analog In' pin. The values are then used to control the blinking rate of an LED. Related example: http://arduino.cc/en/Tutorial/AnalogInput
