# Fritzing sketch AnalogInputPot (saved by Fritzing 0.7.0b)
breadboards: 1

parts:
  Arduino2 = Arduino
  LED2 = LED - 5mm [color="Red (633nm)" package="5 mm [THT]"]
  R1 = Rotary Potentiometer (Large) [maximum_resistance=100kΩ package=THT]

nets:
  N1: Arduino2.GND, LED2.cathode, R1.leg2
  N2: Arduino2.D13, LED2.anode
  N3: Arduino2.+5V, R1.leg1
  N4: Arduino2.A3, R1.wiper

notes:
  In this example, potentiometer values are read in through an 'Analog In' pin. The values are then used to control the blinking rate of an LED. Related example: http://arduino.cc/en/Tutorial/AnalogInput

// code stored in the sketch: ___lockfile___.txt

