# Fritzing sketch AnalogInputThermistor (saved by Fritzing 0.3.15b)
breadboards: 1

parts:
  Arduino2 = Arduino
  R3 = Resistor [resistance=1k package=THT]
  R4 = Temperature Sensor (Thermistor) [package=THT]
  LED2 = Blue LED - 5mm

nets:
  N1: Arduino2.GND, R3.Pin_0, LED2.cathode
  N2: Arduino2.D13, LED2.anode
  N3: Arduino2.+5V, R4.pin_0
  N4: Arduino2.A2, R3.Pin_1, R4.pin_1

notes:
  In this example, thermistor values are read in through an 'Analog In' pin. The values are then used to control the blinking rate of an LED. Using a multimeter, check the min and max resistance of the thermistor in different light conditions. Then calculate the resistor's value with the Axel-Benz formula:
  Rref = sqrt(Rmin*Rmax)
  Related example: http://arduino.cc/en/Tutorial/AnalogInput
