# Fritzing sketch AnalogInputToServo (saved by Fritzing 0.7.0b)
breadboards: 1

parts:
  Arduino2 = Arduino
  J1 = Basic Servo
  R1 = Rotary Potentiometer (Large) [maximum_resistance=100kΩ package=THT]

nets:
  GND: Arduino2.GND, J1.gnd, R1.leg2
  N1: Arduino2.D9, J1.pulse
  +5V: Arduino2.+5V, J1.vcc, R1.leg1
  N2: Arduino2.A2, R1.wiper

notes:
  In this example, potentiometer values are read in through an 'Analog In' pin. The values are then used to control the position of a servo motor. Related examples: http://arduino.cc/en/Tutorial/AnalogInput http://arduino.cc/en/Tutorial/Knob

// code stored in the sketch: ___lockfile___.txt

