# Fritzing sketch Arduino-no-FTDI (saved by Fritzing 0.3.4b)
breadboards: 1

parts:
  C1 = Electrolytic Capacitor [package=THT]
  C2 = Electrolytic Capacitor [package=THT]
  U1 = Voltage Regulator - 5V [package="TO220 [THT]"]
  U2 = atmega168 [package="DIP28 [THT]"]
  R1 = 1k Ω Resistor [package=THT]
  S1 = Pushbutton [package=THT]
  C3 = Ceramic Disk Capacitor [package=THT]
  C4 = Ceramic Disk Capacitor [package=THT]
  XTAL1 = Crystal [package=THT]
  Power_plug1 = Power plug
  J3 = Generic female header - metal rounded - 14 pins [package=THT]
  J3_2 = Generic female header - metal rounded - 14 pins [package=THT]

nets:
  GND: C1.-, C2.-, U1.GND, U2.Pin_8, U2.Pin_22, S1.Pin_3, S1.Pin_4, C3.pin_1, C4.pin_0, Power_plug1.GND, J3.pin7, J3_2.pin8
  N1: C1.+, U1.input_voltage, Power_plug1.VCC
  N2: C2.+, U1.output_voltage, U2.Pin_7, U2.Pin_20, U2.Pin_21, R1.Pin_0, J3.pin8, J3.pin9, J3_2.pin7
  N3: U2.Pin_1, R1.Pin_1, S1.Pin_1, S1.Pin_2, J3_2.pin1
  N4: U2.Pin_2, J3_2.pin2
  N5: U2.Pin_3, J3_2.pin3
  N6: U2.Pin_4, J3_2.pin4
  N7: U2.Pin_5, J3_2.pin5
  N8: U2.Pin_6, J3_2.pin6
  N9: U2.Pin_9, C4.pin_1, XTAL1.pin_0, J3_2.pin9
  N10: U2.Pin_10, C3.pin_0, XTAL1.pin_1, J3_2.pin10
  N11: U2.Pin_11, J3_2.pin11
  N12: U2.Pin_12, J3_2.pin12
  N13: U2.Pin_13, J3_2.pin13
  N14: U2.Pin_14, J3_2.pin14
  N15: U2.Pin_15, J3.pin14
  N16: U2.Pin_16, J3.pin13
  N17: U2.Pin_17, J3.pin12
  N18: U2.Pin_18, J3.pin11
  N19: U2.Pin_19, J3.pin10
  N20: U2.Pin_23, J3.pin6
  N21: U2.Pin_24, J3.pin5
  N22: U2.Pin_25, J3.pin4
  N23: U2.Pin_26, J3.pin3
  N24: U2.Pin_27, J3.pin2
  N25: U2.Pin_28, J3.pin1

notes:
  This is a breadboard Arduino without an FTDI chip. You can program the chip with a USB-Serial breakout board, by using an external programmer or by programming the MCU in an Arduino board and then popping it into this circuit. The power source should be at least 7 VDC. Related example: http://itp.nyu.edu/physcomp/Tutorials/ArduinoBreadboard
