# Fritzing sketch Arduino-no-FTDI (saved by Fritzing 0.7.0b)
breadboards: 1

parts:
  U1 = Voltage Regulator - 5V [package="TO220 [THT]"]
  U2 = atmega168 [package="DIP28 [THT]"]
  Power_plug1 = Power plug
  R2 = Resistor [resistance=1k tolerance=±5% package=THT]
  J4 = female pin header, 14 pins [form="♀ (female rounded)"]
  J5 = female pin header, 14 pins [form="♀ (female rounded)"]
  S2 = Pushbutton [package="[THT]"]
  C2 = Electrolytic Capacitor [capacitance=10µF rated_voltage=35V package="100 mil [THT, electrolytic]"]
  C1 = Electrolytic Capacitor [capacitance=10µF rated_voltage=35V package="100 mil [THT, electrolytic]"]
  C6 = Ceramic Capacitor [capacitance=22pF rated_voltage=35V package="200 mil [THT, multilayer]"]
  C5 = Ceramic Capacitor [capacitance=22pF rated_voltage=35V package="200 mil [THT, multilayer]"]
  XTAL1 = Crystal [frequency="16 Mhz" package=THT]

nets:
  N1: U1.input_voltage, Power_plug1.VCC, C1.+
  GND: U1.GND, U2.Pin_8, U2.Pin_22, Power_plug1.GND, J4.pin7, J5.pin8, S2.Pin_3, S2.Pin_4, C2.-, C1.-, C6.0, C5.1
  N2: U1.output_voltage, U2.Pin_7, U2.Pin_20, U2.Pin_21, R2.Pin_0, J4.pin8, J4.pin9, J5.pin7, C2.+
  N3: U2.Pin_1, R2.Pin_1, J5.pin1, S2.Pin_1, S2.Pin_2
  N4: U2.Pin_2, J5.pin2
  N5: U2.Pin_3, J5.pin3
  N6: U2.Pin_4, J5.pin4
  N7: U2.Pin_5, J5.pin5
  N8: U2.Pin_6, J5.pin6
  N9: U2.Pin_9, J5.pin9, C6.1, XTAL1.pin_0
  N10: U2.Pin_10, J5.pin10, C5.0, XTAL1.pin_1
  N11: U2.Pin_11, J5.pin11
  N12: U2.Pin_12, J5.pin12
  N13: U2.Pin_13, J5.pin13
  N14: U2.Pin_14, J5.pin14
  N15: U2.Pin_15, J4.pin14
  N16: U2.Pin_16, J4.pin13
  N17: U2.Pin_17, J4.pin12
  N18: U2.Pin_18, J4.pin11
  N19: U2.Pin_19, J4.pin10
  N20: U2.Pin_23, J4.pin6
  N21: U2.Pin_24, J4.pin5
  N22: U2.Pin_25, J4.pin4
  N23: U2.Pin_26, J4.pin3
  N24: U2.Pin_27, J4.pin2
  N25: U2.Pin_28, J4.pin1

notes:
  This is a breadboard Arduino without an FTDI chip. You can program the chip with a USB-Serial breakout board, by using an external programmer or by programming the MCU in an Arduino board and then popping it into this circuit. The power source should be at least 7 VDC. Related example: http://itp.nyu.edu/physcomp/Tutorials/ArduinoBreadboard

// code stored in the sketch: ___lockfile___.txt

