# Fritzing sketch Blink-SMD (saved by Fritzing 0.5.3b)

parts:
  Arduino2 = Arduino
  LED1 = Red smd LED [package="0805 [SMD]"]

nets:
  N1: Arduino2.GND, LED1.cathode
  N2: Arduino2.D13, LED1.anode

notes:
  In this very simple example, Arduino will be programmed to blink the LED on pin 13. Related example: http://arduino.cc/en/Tutorial/Blink
