# Fritzing sketch Blink-SMD (saved by Fritzing 0.7.0b)

parts:
  LED1 = smd LED [color="Red (633nm)" package="0805 [SMD]"]
  Arduino2 = Arduino

nets:
  N1: LED1.cathode, Arduino2.GND
  N2: LED1.anode, Arduino2.D13

notes:
  In this very simple example, Arduino will be programmed to blink the LED on pin 13. Related example: http://arduino.cc/en/Tutorial/Blink

// code stored in the sketch: ___lockfile___.txt

