# Fritzing sketch Blink (saved by Fritzing 0.5.0b)

parts:
  Arduino2 = Arduino
  LED2 = Red LED - 5mm [package="5 mm [THT]"]

nets:
  N1: Arduino2.GND, LED2.cathode
  N2: Arduino2.D13, LED2.anode

notes:
  In this very simple example, Arduino will be programmed to blink the LED on pin 13. Related example: http://arduino.cc/en/Tutorial/Blink
