# Fritzing sketch Blink (saved by Fritzing 0.7.0b)

parts:
  Arduino2 = Arduino
  LED1 = LED - 5mm [color="Red (633nm)" package="5 mm [THT]"]

nets:
  N1: Arduino2.GND, LED1.cathode
  N2: Arduino2.D13, LED1.anode

notes:
  In this very simple example, Arduino will be programmed to blink the LED on pin 13. Related example: http://arduino.cc/en/Tutorial/Blink

// code stored in the sketch: ___lockfile___.txt

