# Fritzing sketch Button-SMD (saved by Fritzing 0.5.3b)
breadboards: 1

parts:
  Arduino2 = Arduino
  S1 = Pushbutton [package=THT]
  LED1 = Red smd LED [package="0805 [SMD]"]
  R1 = Resistor [resistance=10k package="0805 [SMD]"]

nets:
  N1: Arduino2.GND, LED1.cathode, R1.Pin_0
  N2: Arduino2.D13, LED1.anode
  N3: Arduino2.D2, S1.leg1, R1.Pin_1
  N4: Arduino2.+5V, S1.leg0

notes:
  In this example, a pushbutton is used as a digital input and an LED is a digital output. Related example: http://arduino.cc/en/Tutorial/Button
