# Fritzing sketch Button-SMD (saved by Fritzing 0.7.0b)
breadboards: 1

parts:
  Arduino2 = Arduino
  S1 = Pushbutton [package=THT]
  R1 = Resistor [resistance=10k tolerance=±5% package="0805 [SMD]"]
  LED1 = smd LED [color="Red (633nm)" package="0805 [SMD]"]

nets:
  N1: Arduino2.GND, R1.Pin_0, LED1.cathode
  N2: Arduino2.D13, LED1.anode
  N3: Arduino2.D2, S1.leg1, R1.Pin_1
  N4: Arduino2.+5V, S1.leg0

notes:
  In this example, a pushbutton is used as a digital input and an LED is a digital output. Related example: http://arduino.cc/en/Tutorial/Button

// code stored in the sketch: ___lockfile___.txt

