# Fritzing sketch Button (saved by Fritzing 0.3.12b)
breadboards: 1

parts:
  Arduino2 = Arduino
  R2 = Resistor [resistance=10k package=THT]
  S2 = Pushbutton [package=THT]
  LED2 = Red LED - 5mm

nets:
  N1: Arduino2.GND, R2.Pin_0, LED2.cathode
  N2: Arduino2.D13, LED2.anode
  N3: Arduino2.D2, R2.Pin_1, S2.leg1
  N4: Arduino2.+5V, S2.leg0

notes:
  In this example, a pushbutton is used as a digital input and an LED is a digital output. Related example: http://arduino.cc/en/Tutorial/Button
