# Fritzing sketch CosmicRayGun (saved by Fritzing 0.6.4b)
breadboards: 1

parts:
  Arduino = Arduino
  LED1 = green LED - 5mm [package="5 mm [THT]"]
  R6 = Resistor [resistance=220 tolerance=±5% package=THT]
  LED2 = green LED - 5mm [package="5 mm [THT]"]
  R5 = Resistor [resistance=220 tolerance=±5% package=THT]
  LED3 = yellow LED - 5mm [package="5 mm [THT]"]
  R4 = Resistor [resistance=220 tolerance=±5% package=THT]
  LED4 = yellow LED - 5mm [package="5 mm [THT]"]
  R3 = Resistor [resistance=220 tolerance=±5% package=THT]
  LED5 = Red LED - 5mm [package="5 mm [THT]"]
  R2 = Resistor [resistance=220 tolerance=±5% package=THT]
  LED6 = Red LED - 5mm [package="5 mm [THT]"]
  R1 = Resistor [resistance=220 tolerance=±5% package=THT]
  S2 = Pushbutton [package=THT]
  R7 = Resistor [resistance=1k tolerance=±5% package=THT]
  R8 = Resistor [resistance=1k tolerance=±5% package=THT]
  S1 = Pushbutton [package=THT]
  Speaker = Piezo Speaker

nets:
  N1: Arduino.GND, LED1.cathode, LED2.cathode, LED3.cathode, LED4.cathode, LED5.cathode, LED6.cathode, R7.Pin_0, R8.Pin_0
  N2: Arduino.D13, R8.Pin_1, S1.leg0
  N3: Arduino.D12, R1.Pin_0
  N4: Arduino.D11, R2.Pin_0
  N5: Arduino.D10, R3.Pin_0
  N6: Arduino.D9, R4.Pin_0
  N7: Arduino.D8, R5.Pin_0
  N8: Arduino.D7, R6.Pin_0
  N9: Arduino.D5, S2.leg1, R7.Pin_1
  N10: Arduino.D3, Speaker.pin2
  N11: Arduino.D2, Speaker.pin1
  N12: Arduino.+5V, S2.leg0, S1.leg1
  N13: LED1.anode, R6.Pin_1
  N14: LED2.anode, R5.Pin_1
  N15: LED3.anode, R4.Pin_1
  N16: LED4.anode, R3.Pin_1
  N17: LED5.anode, R2.Pin_1
  N18: LED6.anode, R1.Pin_1

notes:
  Get the code from the Fritzing Project Page:
  Cosmic Raygun
