# Fritzing sketch CosmicRayGun (saved by Fritzing 0.7.0b)
breadboards: 1

parts:
  R6 = Resistor [resistance=220 tolerance=±5% package=THT]
  R5 = Resistor [resistance=220 tolerance=±5% package=THT]
  R4 = Resistor [resistance=220 tolerance=±5% package=THT]
  R3 = Resistor [resistance=220 tolerance=±5% package=THT]
  R2 = Resistor [resistance=220 tolerance=±5% package=THT]
  R1 = Resistor [resistance=220 tolerance=±5% package=THT]
  S2 = Pushbutton [package=THT]
  R7 = Resistor [resistance=1k tolerance=±5% package=THT]
  R8 = Resistor [resistance=1k tolerance=±5% package=THT]
  S1 = Pushbutton [package=THT]
  Speaker = Piezo Speaker
  LED5 = LED - 5mm [color="Red (633nm)" package="5 mm [THT]"]
  LED6 = LED - 5mm [color="Red (633nm)" package="5 mm [THT]"]
  LED3 = LED - 5mm [color="Yellow (585nm)" package="5 mm [THT]"]
  LED1 = LED - 5mm [color="Green (555nm)" package="5 mm [THT]"]
  LED4 = LED - 5mm [color="Yellow (585nm)" package="5 mm [THT]"]
  LED2 = LED - 5mm [color="Green (555nm)" package="5 mm [THT]"]
  Arduino = Arduino

nets:
  N1: R6.Pin_0, Arduino.D7
  N2: R6.Pin_1, LED1.anode
  N3: R5.Pin_0, Arduino.D8
  N4: R5.Pin_1, LED2.anode
  N5: R4.Pin_0, Arduino.D9
  N6: R4.Pin_1, LED3.anode
  N7: R3.Pin_0, Arduino.D10
  N8: R3.Pin_1, LED4.anode
  N9: R2.Pin_0, Arduino.D11
  N10: R2.Pin_1, LED5.anode
  N11: R1.Pin_0, Arduino.D12
  N12: R1.Pin_1, LED6.anode
  N13: S2.leg0, S1.leg1, Arduino.+5V
  N14: S2.leg1, R7.Pin_1, Arduino.D5
  N15: R7.Pin_0, R8.Pin_0, LED5.cathode, LED6.cathode, LED3.cathode, LED1.cathode, LED4.cathode, LED2.cathode, Arduino.GND
  N16: R8.Pin_1, S1.leg0, Arduino.D13
  N17: Speaker.pin1, Arduino.D2
  N18: Speaker.pin2, Arduino.D3

notes:
  Get the code from the Fritzing Project Page:
  Cosmic Raygun

// code stored in the sketch: ___lockfile___.txt

