# Fritzing sketch Countdown (saved by Fritzing 0.7.0b)
breadboards: 1

parts:
  Segment1 = 7 Segment Display
  Segment2 = 7 Segment Display
  Q1 = NPN-Transistor [package="TO92 [THT]"]
  Q2 = PNP-Transistor [package="TO92 [THT]"]
  R1 = Resistor [tolerance=±5% resistance=1k package=THT]
  R2 = Resistor [tolerance=±5% resistance=1k package=THT]
  Q3 = PNP-Transistor [package="TO92 [THT]"]
  Q4 = NPN-Transistor [package="TO92 [THT]"]
  R3 = Resistor [tolerance=±5% resistance=1k package=THT]
  R4 = Resistor [tolerance=±5% resistance=1k package=THT]
  RE1 = Rotary Encoder [package=THT]
  S1 = Pushbutton [package="[THT]"]
  R5 = Resistor [tolerance=±5% resistance=10k package=THT]
  Arduino1 = Arduino

nets:
  N1: Segment1.Segment_E, Segment2.Segment_E, Arduino1.D12
  N2: Segment1.Segment_D, Segment2.Segment_D, Arduino1.D11
  N3: Segment1.common_anode, Q2.C
  N4: Segment1.Segment_C, Segment2.Segment_C, Arduino1.D9
  N5: Segment1.Segment_DP, Segment2.Segment_DP, Arduino1.D8
  N6: Segment1.Segment_B, Segment2.Segment_B, Arduino1.D3
  N7: Segment1.Segment_A, Segment2.Segment_A, Arduino1.D4
  N8: Segment1.Segment_F, Segment2.Segment_F, Arduino1.D5
  N9: Segment1.Segment_G, Segment2.Segment_G, Arduino1.D6
  N10: Segment2.common_anode, Q3.C
  N11: Q1.E, Q4.E, RE1.EncoderPinC, R5.Pin_0, Arduino1.GND
  N12: Q1.B, R1.Pin_0
  N13: Q1.C, R2.Pin_0
  N14: Q2.E, Q3.E, S1.Pin_1, S1.Pin_2, Arduino1.+5V
  N15: Q2.B, R2.Pin_1
  N16: R1.Pin_1, Arduino1.D10
  N17: Q3.B, R4.Pin_1
  N18: Q4.B, R3.Pin_1
  N19: Q4.C, R4.Pin_0
  N20: R3.Pin_0, Arduino1.D7
  N21: RE1.EncoderPinA, Arduino1.A1
  N22: RE1.EncoderPinB, Arduino1.A0
  N23: S1.Pin_3, S1.Pin_4, R5.Pin_1, Arduino1.D2

// code stored in the sketch: ___lockfile___.txt

