# Fritzing sketch Curvy-Parking-Assistant (saved by Fritzing 0.7.0b)
breadboards: 1

parts:
  IR_Sensor_1 = Infrared Proximity Sensor
  Parking_Assistant = Arduino
  IR_Sensor_2 = Infrared Proximity Sensor
  220Ω = Resistor [resistance=220 tolerance=±5% package=THT]
  220Ω_2 = Resistor [resistance=220 tolerance=±5% package=THT]
  220Ω_3 = Resistor [resistance=220 tolerance=±5% package=THT]
  220Ω_4 = Resistor [resistance=220 tolerance=±5% package=THT]
  220Ω_5 = Resistor [resistance=220 tolerance=±5% package=THT]
  220Ω_6 = Resistor [resistance=220 tolerance=±5% package=THT]
  220Ω_7 = Resistor [resistance=220 tolerance=±5% package=THT]
  220Ω_8 = Resistor [resistance=220 tolerance=±5% package=THT]
  220Ω_9 = Resistor [resistance=220 tolerance=±5% package=THT]
  220Ω_10 = Resistor [resistance=220 tolerance=±5% package=THT]
  LED5 = LED - 5mm [color="Red (633nm)" package="5 mm [THT]"]
  LED6 = LED - 5mm [color="Red (633nm)" package="5 mm [THT]"]
  LED2 = LED - 5mm [color="Yellow (585nm)" package="5 mm [THT]"]
  LED4 = LED - 5mm [color="Red (633nm)" package="5 mm [THT]"]
  LED3 = LED - 5mm [color="Red (633nm)" package="5 mm [THT]"]
  LED2_2 = LED - 5mm [color="Yellow (585nm)" package="5 mm [THT]"]
  LED2_3 = LED - 5mm [color="Yellow (585nm)" package="5 mm [THT]"]
  LED2_4 = LED - 5mm [color="Yellow (585nm)" package="5 mm [THT]"]
  LED2_5 = LED - 5mm [color="Yellow (585nm)" package="5 mm [THT]"]
  LED2_6 = LED - 5mm [color="Yellow (585nm)" package="5 mm [THT]"]

nets:
  N1: IR_Sensor_1.Vout, Parking_Assistant.A1
  GND: IR_Sensor_1.GND, Parking_Assistant.GND, IR_Sensor_2.GND, LED5.cathode, LED6.cathode, LED2.cathode, LED4.cathode, LED3.cathode, LED2_2.cathode, LED2_3.cathode, LED2_4.cathode, LED2_5.cathode, LED2_6.cathode
  5V: IR_Sensor_1.Vcc, Parking_Assistant.+5V, IR_Sensor_2.Vcc
  N2: Parking_Assistant.D12, 220Ω.Pin_1
  N3: Parking_Assistant.D11, 220Ω_2.Pin_1
  N4: Parking_Assistant.D10, 220Ω_3.Pin_1
  N5: Parking_Assistant.D9, 220Ω_5.Pin_1
  N6: Parking_Assistant.D8, 220Ω_4.Pin_1
  N7: Parking_Assistant.D6, 220Ω_6.Pin_1
  N8: Parking_Assistant.D5, 220Ω_7.Pin_1
  N9: Parking_Assistant.D4, 220Ω_10.Pin_1
  N10: Parking_Assistant.D3, 220Ω_8.Pin_1
  N11: Parking_Assistant.D2, 220Ω_9.Pin_1
  N12: Parking_Assistant.A0, IR_Sensor_2.Vout
  N13: 220Ω.Pin_0, LED6.anode
  N14: 220Ω_2.Pin_0, LED5.anode
  N15: 220Ω_3.Pin_0, LED2_2.anode
  N16: 220Ω_4.Pin_0, LED2_6.anode
  N17: 220Ω_5.Pin_0, LED2_5.anode
  N18: 220Ω_6.Pin_0, LED2_3.anode
  N19: 220Ω_7.Pin_0, LED2_4.anode
  N20: 220Ω_8.Pin_0, LED3.anode
  N21: 220Ω_9.Pin_0, LED4.anode
  N22: 220Ω_10.Pin_0, LED2.anode

notes:
  Simple Parking Assistant
  The distance to objects in the proximity is measured and displayed as led graph.

// code stored in the sketch: ___lockfile___.txt

