# Fritzing sketch DC_motor_control (saved by Fritzing 0.7.0b)
breadboards: 1

parts:
  IC1 = H-Bridge [package=THT]
  R2 = Resistor [resistance=1k tolerance=±5% package=THT]
  S2 = Pushbutton [package=THT]
  M1 = DC Motor
  Arduino2 = Arduino

nets:
  N1: IC1.1_2EN, Arduino2.D4
  N2: IC1.1A, Arduino2.D5
  N3: IC1.1Y, M1.pin_1
  GND1: IC1.GND1, IC1.GND2, IC1.GND3, IC1.GND4, R2.Pin_0, Arduino2.GND
  N4: IC1.2Y, M1.pin_2
  N5: IC1.2A, Arduino2.D12
  N6: IC1.VCC2, Arduino2.3V3
  N7: IC1.VCC1, S2.leg0, Arduino2.+5V
  N8: R2.Pin_1, S2.leg1, Arduino2.D2

notes:
  This project shows how to control a DC motor's direction (running forwards and backwards) using an H-bridge. An H-bridge is an electronic circuit which enables a voltage to be applied across a load in either direction.
  http://itp.nyu.edu/physcomp/Labs/DCMotorControl

// code stored in the sketch: ___lockfile___.txt

