# Fritzing sketch EDGY-motor-control (saved by Fritzing 0.7.0b)
breadboards: 1

parts:
  Arduino1 = Arduino
  EDGY_motor_control1 = EDGY
  M1 = DC Motor

nets:
  N1: Arduino1.D5, EDGY_motor_control1.A1
  N2: Arduino1.D4, EDGY_motor_control1.B1
  N3: Arduino1.D3, EDGY_motor_control1.Speed1
  +5V: Arduino1.+5V, EDGY_motor_control1.Vin, EDGY_motor_control1.5V+
  GND: Arduino1.GND, EDGY_motor_control1.GND
  N4: EDGY_motor_control1.B1out, M1.pin_2
  N5: EDGY_motor_control1.A1out, M1.pin_1

// code stored in the sketch: ___lockfile___.txt

