# Fritzing sketch Knock (saved by Fritzing 0.3.4b)
breadboards: 1

parts:
  Arduino1 = Arduino
  J1 = Piezo Speaker
  R3 = 1M Ω Resistor [package=THT]

nets:
  N1: Arduino1.GND, J1.pin1, R3.Pin_0
  N2: Arduino1.A0, J1.pin2, R3.Pin_1

notes:
  A Piezo is an electronic device that can both be used to play tones and to detect tones. In this project, a Piezo captures a knock and sends a string "Knock!" back to the computer over the serial port. In order to see this text you can use the Arduino serial monitor.
  http://arduino.cc/en/Tutorial/Knock
