# Fritzing sketch Knock (saved by Fritzing 0.7.0b)
breadboards: 1

parts:
  Arduino1 = Arduino
  J1 = Piezo Speaker
  R4 = Resistor [resistance=1M tolerance=±5% package=THT]

nets:
  N1: Arduino1.GND, J1.pin1, R4.Pin_0
  N2: Arduino1.A0, J1.pin2, R4.Pin_1

notes:
  A Piezo is an electronic device that can both be used to play tones and to detect tones. In this project, a Piezo captures a knock and sends a string "Knock!" back to the computer over the serial port. In order to see this text you can use the Arduino serial monitor.
  http://arduino.cc/en/Tutorial/Knock

// code stored in the sketch: ___lockfile___.txt

