# Fritzing sketch LiquidCrystalDisplay (saved by Fritzing 0.6.3b)
breadboards: 1

parts:
  LCD = LCD screen
  LCD_Shield = Arduino
  Contrast = Rotary Potentiometer (Small) [maximum_resistance=100kΩ]

nets:
  GND: LCD.VSS, LCD.R/W, LCD.LED-, LCD_Shield.GND, Contrast.leg1
  5V: LCD.VDD, LCD.LED+, LCD_Shield.+5V, Contrast.leg2
  N1: LCD.V0, Contrast.wiper
  N2: LCD.RS, LCD_Shield.D12
  N3: LCD.E, LCD_Shield.D11
  N4: LCD.DB4, LCD_Shield.D5
  N5: LCD.DB5, LCD_Shield.D4
  N6: LCD.DB6, LCD_Shield.D3
  N7: LCD.DB7, LCD_Shield.D2

notes:
  Code and more on character LCDs at http://arduino.cc/en/Tutorial/LiquidCrystal
