# Fritzing sketch LiquidCrystalDisplay (saved by Fritzing 0.7.0b)
breadboards: 1

parts:
  LCD_Shield = Arduino
  Contrast = Rotary Potentiometer (Small) [maximum_resistance=100kΩ]
  LCD = LCD screen
  R1 = Resistor [tolerance=±5% resistance=220 package=THT]

nets:
  GND: LCD_Shield.GND, Contrast.leg1, LCD.VSS, LCD.R/W, LCD.LED-
  N1: LCD_Shield.D12, LCD.RS
  N2: LCD_Shield.D11, LCD.E
  N3: LCD_Shield.D5, LCD.DB4
  N4: LCD_Shield.D4, LCD.DB5
  N5: LCD_Shield.D3, LCD.DB6
  N6: LCD_Shield.D2, LCD.DB7
  5V: LCD_Shield.+5V, Contrast.leg2, LCD.VDD, R1.Pin_1
  N7: Contrast.wiper, LCD.V0
  N8: LCD.LED+, R1.Pin_0

notes:
  Code and more on character LCDs at http://arduino.cc/en/Tutorial/LiquidCrystal

// code stored in the sketch: ___lockfile___.txt

