# Fritzing sketch Loop-SMD (saved by Fritzing 0.5.3b)
breadboards: 1

parts:
  Arduino = Arduino
  LED3 = Red smd LED [package="0805 [SMD]"]
  LED4 = Red smd LED [package="0805 [SMD]"]
  LED5 = Red smd LED [package="0805 [SMD]"]
  LED6 = Red smd LED [package="0805 [SMD]"]
  LED1 = Red smd LED [package="0805 [SMD]"]
  LED2 = Red smd LED [package="0805 [SMD]"]
  R1 = Resistor [resistance=220 package="0805 [SMD]"]
  R2 = Resistor [resistance=220 package="0805 [SMD]"]
  R3 = Resistor [resistance=220 package="0805 [SMD]"]
  R4 = Resistor [resistance=220 package="0805 [SMD]"]
  R5 = Resistor [resistance=220 package="0805 [SMD]"]
  R6 = Resistor [resistance=220 package="0805 [SMD]"]

nets:
  N1: Arduino.GND, LED3.cathode, LED4.cathode, LED5.cathode, LED6.cathode, LED1.cathode, LED2.cathode
  N2: Arduino.D7, R6.Pin_1
  N3: Arduino.D6, R5.Pin_1
  N4: Arduino.D5, R4.Pin_1
  N5: Arduino.D4, R3.Pin_1
  N6: Arduino.D3, R2.Pin_1
  N7: Arduino.D2, R1.Pin_1
  N8: LED3.anode, R3.Pin_0
  N9: LED4.anode, R4.Pin_0
  N10: LED5.anode, R5.Pin_0
  N11: LED6.anode, R6.Pin_0
  N12: LED1.anode, R1.Pin_0
  N13: LED2.anode, R2.Pin_0

notes:
  In this example, six leds are controlled by digital out pins. Related Example: http://arduino.cc/en/Tutorial/Loop
