# Fritzing sketch Loop-SMD (saved by Fritzing 0.7.0b)
breadboards: 1

parts:
  Arduino = Arduino
  R1 = Resistor [resistance=220 tolerance=±5% package="0805 [SMD]"]
  R2 = Resistor [resistance=220 tolerance=±5% package="0805 [SMD]"]
  R3 = Resistor [resistance=220 tolerance=±5% package="0805 [SMD]"]
  R4 = Resistor [resistance=220 tolerance=±5% package="0805 [SMD]"]
  R5 = Resistor [resistance=220 tolerance=±5% package="0805 [SMD]"]
  R6 = Resistor [resistance=220 tolerance=±5% package="0805 [SMD]"]
  LED1 = smd LED [color="Red (633nm)" package="0805 [SMD]"]
  LED2 = smd LED [color="Red (633nm)" package="0805 [SMD]"]
  LED4 = smd LED [color="Red (633nm)" package="0805 [SMD]"]
  LED5 = smd LED [color="Red (633nm)" package="0805 [SMD]"]
  LED3 = smd LED [color="Red (633nm)" package="0805 [SMD]"]
  LED6 = smd LED [color="Red (633nm)" package="0805 [SMD]"]

nets:
  N1: Arduino.GND, LED1.cathode, LED2.cathode, LED4.cathode, LED5.cathode, LED3.cathode, LED6.cathode
  N2: Arduino.D7, R6.Pin_1
  N3: Arduino.D6, R5.Pin_1
  N4: Arduino.D5, R4.Pin_1
  N5: Arduino.D4, R3.Pin_1
  N6: Arduino.D3, R2.Pin_1
  N7: Arduino.D2, R1.Pin_1
  N8: R1.Pin_0, LED1.anode
  N9: R2.Pin_0, LED2.anode
  N10: R3.Pin_0, LED3.anode
  N11: R4.Pin_0, LED4.anode
  N12: R5.Pin_0, LED5.anode
  N13: R6.Pin_0, LED6.anode

notes:
  In this example, six leds are controlled by digital out pins. Related Example: http://arduino.cc/en/Tutorial/Loop

// code stored in the sketch: ___lockfile___.txt

