# Fritzing sketch Loop (saved by Fritzing 0.3.9b)
breadboards: 1

parts:
  LED1 = Red LED - 5mm
  LED2 = Red LED - 5mm
  LED3 = Red LED - 5mm
  LED4 = Red LED - 5mm
  LED5 = Red LED - 5mm
  LED6 = Red LED - 5mm
  Arduino = Arduino
  R7 = Resistor [resistance=220 package=THT]
  R8 = Resistor [resistance=220 package=THT]
  R9 = Resistor [resistance=220 package=THT]
  R10 = Resistor [resistance=220 package=THT]
  R11 = Resistor [resistance=220 package=THT]
  R12 = Resistor [resistance=220 package=THT]

nets:
  N1: LED1.cathode, LED2.cathode, LED3.cathode, LED4.cathode, LED5.cathode, LED6.cathode, Arduino.GND
  N2: LED1.anode, R12.Pin_0
  N3: LED2.anode, R11.Pin_0
  N4: LED3.anode, R7.Pin_0
  N5: LED4.anode, R8.Pin_0
  N6: LED5.anode, R10.Pin_0
  N7: LED6.anode, R9.Pin_0
  N8: Arduino.D7, R12.Pin_1
  N9: Arduino.D6, R11.Pin_1
  N10: Arduino.D5, R7.Pin_1
  N11: Arduino.D4, R8.Pin_1
  N12: Arduino.D3, R10.Pin_1
  N13: Arduino.D2, R9.Pin_1

notes:
  In this example, six leds are controlled by digital out pins. Related Example: http://arduino.cc/en/Tutorial/Loop
