# Fritzing sketch Loop (saved by Fritzing 0.7.0b)
breadboards: 1

parts:
  Arduino = Arduino
  R4 = Resistor [resistance=220 tolerance=±5% package=THT]
  R3 = Resistor [resistance=220 tolerance=±5% package=THT]
  R1 = Resistor [resistance=220 tolerance=±5% package=THT]
  R2 = Resistor [resistance=220 tolerance=±5% package=THT]
  R5 = Resistor [resistance=220 tolerance=±5% package=THT]
  R6 = Resistor [resistance=220 tolerance=±5% package=THT]
  LED3 = LED - 5mm [color="Red (633nm)" package="5 mm [THT]"]
  LED1 = LED - 5mm [color="Red (633nm)" package="5 mm [THT]"]
  LED6 = LED - 5mm [color="Red (633nm)" package="5 mm [THT]"]
  LED2 = LED - 5mm [color="Red (633nm)" package="5 mm [THT]"]
  LED5 = LED - 5mm [color="Red (633nm)" package="5 mm [THT]"]
  LED4 = LED - 5mm [color="Red (633nm)" package="5 mm [THT]"]

nets:
  N1: Arduino.GND, LED3.cathode, LED1.cathode, LED6.cathode, LED2.cathode, LED5.cathode, LED4.cathode
  N2: Arduino.D7, R6.Pin_1
  N3: Arduino.D6, R5.Pin_1
  N4: Arduino.D5, R4.Pin_1
  N5: Arduino.D4, R3.Pin_1
  N6: Arduino.D3, R2.Pin_1
  N7: Arduino.D2, R1.Pin_1
  N8: R4.Pin_0, LED4.anode
  N9: R3.Pin_0, LED3.anode
  N10: R1.Pin_0, LED1.anode
  N11: R2.Pin_0, LED2.anode
  N12: R5.Pin_0, LED5.anode
  N13: R6.Pin_0, LED6.anode

notes:
  In this example, six leds are controlled by digital out pins. Related Example: http://arduino.cc/en/Tutorial/Loop

// code stored in the sketch: ___lockfile___.txt

