# Fritzing sketch Melody (saved by Fritzing 0.7.0b)

parts:
  Arduino1 = Arduino
  J1 = Piezo Speaker

nets:
  N1: Arduino1.GND, J1.pin1
  N2: Arduino1.D9, J1.pin2

notes:
  Piezoelectric speakers are frequently used as beepers in watches and other electronic devices. In this project, a piezo speaker is used to play melodies. It sends a square wave of the appropriate frequency to the piezo, generating the corresponding tone.
  http://arduino.cc/en/Tutorial/Melody

// code stored in the sketch: ___lockfile___.txt

