# Fritzing sketch MidiDrumKit (saved by Fritzing 0.7.0b)
breadboards: 1

parts:
  MIDI_Drum_Kit = Arduino
  J1 = Piezo Speaker
  J1_2 = Piezo Speaker
  R1 = Resistor [resistance=1M tolerance=±5% package=THT]
  R1_2 = Resistor [resistance=1M tolerance=±5% package=THT]
  Zener1 = Rectifier Diode [part_number=1N4001 package="300 mil [THT]"]
  Zener2 = Rectifier Diode [part_number=1N4001 package="300 mil [THT]"]
  S1 = Pushbutton [package="[THT]"]
  S2 = Pushbutton [package="[THT]"]
  S3 = Pushbutton [package="[THT]"]
  R1_3 = Resistor [resistance=100k tolerance=±5% package=THT]
  R1_4 = Resistor [resistance=100k tolerance=±5% package=THT]
  R1_5 = Resistor [resistance=100k tolerance=±5% package=THT]
  DIN1 = DIN-5 jack (MIDI) [package=THT]
  R2 = Resistor [resistance=220 tolerance=±5% package=THT]

nets:
  GND: MIDI_Drum_Kit.GND, J1.pin1, J1_2.pin1, R1.Pin_1, R1_2.Pin_1, Zener1.anode, Zener2.anode, S1.Pin_3, S1.Pin_4, S2.Pin_3, S2.Pin_4, S3.Pin_3, S3.Pin_4, R1_3.Pin_1, R1_4.Pin_1, R1_5.Pin_1, DIN1.2
  N1: MIDI_Drum_Kit.D7, S1.Pin_1, S1.Pin_2, R1_3.Pin_0
  N2: MIDI_Drum_Kit.D6, S2.Pin_1, S2.Pin_2, R1_4.Pin_0
  N3: MIDI_Drum_Kit.D5, S3.Pin_1, S3.Pin_2, R1_5.Pin_0
  N4: MIDI_Drum_Kit.D1TX, DIN1.5
  5V: MIDI_Drum_Kit.+5V, R2.Pin_1
  N5: MIDI_Drum_Kit.A0, J1_2.pin2, R1_2.Pin_0, Zener2.cathode
  N6: MIDI_Drum_Kit.A1, J1.pin2, R1.Pin_0, Zener1.cathode
  N7: DIN1.4, R2.Pin_0

notes:
  Arduino MIDI Drum Shield
  from todbot.com
  Diodes should be 5.1 V Zener diodes

// code stored in the sketch: ___lockfile___.txt

