# Fritzing sketch Mood-Light (saved by Fritzing 0.7.0b)
breadboards: 1

parts:
  R1 = Resistor [tolerance=±5% resistance=220 package=THT]
  R2 = Resistor [tolerance=±5% resistance=220 package=THT]
  R3 = Resistor [tolerance=±5% resistance=220 package=THT]
  Arduino1 = Arduino

nets:
  N1: R1.Pin_0, Arduino1.D12
  N2: R2.Pin_1, Arduino1.D11
  N3: R3.Pin_1, Arduino1.D10
