# Fritzing sketch Mood-Light (saved by Fritzing 0.7.0b)
breadboards: 1

parts:
  LED1 = Super Flux RGB LED (com. anode)
  R1 = Resistor [tolerance=±5% resistance=220 package=THT]
  R2 = Resistor [tolerance=±5% resistance=220 package=THT]
  R3 = Resistor [tolerance=±5% resistance=220 package=THT]
  Arduino1 = Arduino

nets:
  N1: LED1.red_cathode, R1.Pin_1
  N2: LED1.blue_cathode, R2.Pin_0
  N3: LED1.green_cathode, R3.Pin_0
  N4: LED1.common_anode, Arduino1.+5V
  N5: R1.Pin_0, Arduino1.D12
  N6: R2.Pin_1, Arduino1.D11
  N7: R3.Pin_1, Arduino1.D10

// code stored in the sketch: ___lockfile___.txt

