# Fritzing sketch Op-amp (saved by Fritzing 0.7.0b)
breadboards: 1

parts:
  Arduino1 = Arduino
  U1 = LM 358 Dual Op-Amp [package="DIP8 [THT]"]
  J1 = Basic Force Sensing Resistor (FSR) [package=THT]
  R3 = Resistor [resistance=6.8k tolerance=±5% package=THT]

nets:
  N1: Arduino1.GND, U1.connector3, R3.Pin_1
  N2: Arduino1.+5V, U1.connector7, J1.pin_0
  N3: Arduino1.A2, U1.connector0, U1.connector1
  N4: U1.connector2, J1.pin_1, R3.Pin_0

notes:
  In this example, an LM 358 Dual Operational Amplifier is used to get a stronger, more stable signal from an FSR. You can use this configuration with any resistive sensor. Feel free to place a small ceramic cap between PIN1 on the Opamp and GND to make the signal smoother.
  http://itp.nyu.edu/physcomp/sensors/Schematics/LM358OpAmp

// code stored in the sketch: ___lockfile___.txt

