# Fritzing sketch Optocoupler (saved by Fritzing 0.3.15b)
breadboards: 1

parts:
  U1 = Optocoupler [package=THT]
  VCC1 = obsolete Battery
  Arduino2 = Arduino
  R3 = Resistor [resistance=220 package=THT]
  LED2 = Red LED - 5mm
  R4 = Resistor [resistance=220 package=THT]

nets:
  N1: U1.Pin_1, R3.Pin_1
  N2: U1.Pin_2, Arduino2.GND
  N3: U1.Pin_4, VCC1.-
  N4: U1.Pin_5, LED2.cathode
  N5: VCC1.+, R4.Pin_1
  N6: Arduino2.D11, R3.Pin_0
  N7: LED2.anode, R4.Pin_0

notes:
  An optocoupler can be used to control a circuit that's completely isolated from your microcontroller in order to avoid the risk of short-circuit. In this case, imagine that the LED + battery pack combo is a hacked toy that you're turning on and off with the Arduino.
