# Fritzing sketch Parking-Assistant (saved by Fritzing 0.3.13b)
breadboards: 1

parts:
  IR_Sensor_1 = Infrared Proximity Sensor
  Parking_Assistant = Arduino
  LED2 = yellow LED - 5mm
  LED2_2 = yellow LED - 5mm
  LED2_3 = yellow LED - 5mm
  LED2_4 = yellow LED - 5mm
  LED2_5 = yellow LED - 5mm
  LED2_6 = yellow LED - 5mm
  LED3 = Red LED - 5mm
  LED4 = Red LED - 5mm
  LED5 = Red LED - 5mm
  LED6 = Red LED - 5mm
  IR_Sensor_2 = Infrared Proximity Sensor
  220Ω = Resistor [resistance=220 package=THT]
  220Ω_2 = Resistor [resistance=220 package=THT]
  220Ω_3 = Resistor [resistance=220 package=THT]
  220Ω_4 = Resistor [resistance=220 package=THT]
  220Ω_5 = Resistor [resistance=220 package=THT]
  220Ω_6 = Resistor [resistance=220 package=THT]
  220Ω_7 = Resistor [resistance=220 package=THT]
  220Ω_8 = Resistor [resistance=220 package=THT]
  220Ω_9 = Resistor [resistance=220 package=THT]
  220Ω_10 = Resistor [resistance=220 package=THT]

nets:
  N1: IR_Sensor_1.Vout, Parking_Assistant.A1
  GND: IR_Sensor_1.GND, Parking_Assistant.GND, LED2.cathode, LED2_2.cathode, LED2_3.cathode, LED2_4.cathode, LED2_5.cathode, LED2_6.cathode, LED3.cathode, LED4.cathode, LED5.cathode, LED6.cathode, IR_Sensor_2.GND
  5V: IR_Sensor_1.Vcc, Parking_Assistant.+5V, IR_Sensor_2.Vcc
  N2: Parking_Assistant.D12, 220Ω.Pin_1
  N3: Parking_Assistant.D11, 220Ω_2.Pin_1
  N4: Parking_Assistant.D10, 220Ω_3.Pin_1
  N5: Parking_Assistant.D9, 220Ω_5.Pin_1
  N6: Parking_Assistant.D8, 220Ω_4.Pin_1
  N7: Parking_Assistant.D6, 220Ω_6.Pin_1
  N8: Parking_Assistant.D5, 220Ω_7.Pin_1
  N9: Parking_Assistant.D4, 220Ω_10.Pin_1
  N10: Parking_Assistant.D3, 220Ω_8.Pin_1
  N11: Parking_Assistant.D2, 220Ω_9.Pin_1
  N12: Parking_Assistant.A0, IR_Sensor_2.Vout
  N13: LED2.anode, 220Ω_3.Pin_0
  N14: LED2_2.anode, 220Ω_5.Pin_0
  N15: LED2_3.anode, 220Ω_4.Pin_0
  N16: LED2_4.anode, 220Ω_6.Pin_0
  N17: LED2_5.anode, 220Ω_7.Pin_0
  N18: LED2_6.anode, 220Ω_10.Pin_0
  N19: LED3.anode, 220Ω_8.Pin_0
  N20: LED4.anode, 220Ω_9.Pin_0
  N21: LED5.anode, 220Ω_2.Pin_0
  N22: LED6.anode, 220Ω.Pin_0

notes:
  Simple Parking Assistant
  The distance to objects in the proximity is measured and displayed as led graph.
