# Fritzing sketch Photocell (saved by Fritzing 0.3.9b)
breadboards: 1

parts:
  R_1 = Basic Photo-Resistor (Photocell) [package=THT]
  LED1 = Red LED - 5mm
  Arduino1 = Arduino
  R4 = Resistor [resistance=10k package=THT]

nets:
  N1: R_1.pin_0, Arduino1.+5V
  N2: R_1.pin_1, Arduino1.A2, R4.Pin_0
  N3: LED1.cathode, Arduino1.GND, R4.Pin_1
  N4: LED1.anode, Arduino1.D13

notes:
  In this example, photocell values are read in through an 'Analog In' pin. The values are then used to control the blinking rate of an LED.
  Using a multimeter, check the min and max resistance of the thermistor in different light conditions. Then calculate the resistor's value with the Axel-Benz formula: Rref = sqrt(Rmin*Rmax)
  Related example: http://www.ladyada.net/learn/sensors/cds.html
