# Fritzing sketch Photocell (saved by Fritzing 0.7.0b)
breadboards: 1

parts:
  Arduino1 = Arduino
  R4 = Resistor [resistance=10k tolerance=±5% package=THT]
  R5 = Photocell (LDR) [package=THT]
  LED2 = LED - 5mm [color="Red (633nm)" package="5 mm [THT]"]

nets:
  N1: Arduino1.GND, R4.Pin_1, LED2.cathode
  N2: Arduino1.D13, LED2.anode
  N3: Arduino1.+5V, R5.pin_0
  N4: Arduino1.A2, R4.Pin_0, R5.pin_1

notes:
  In this example, photocell values are read in through an 'Analog In' pin. The values are then used to control the blinking rate of an LED.
  Using a multimeter, check the min and max resistance of the photocell in different light conditions. Then calculate the resistor's value with the Axel-Benz formula: Rref = sqrt(Rmin*Rmax)
  Related example: http://www.ladyada.net/learn/sensors/cds.html

// code stored in the sketch: ___lockfile___.txt

