# Fritzing sketch RGB-LED (saved by Fritzing 0.7.0b)
breadboards: 1

parts:
  RGB_Shield = Arduino
  R1 = Resistor [resistance=180 tolerance=±5% package=THT]
  R3 = Resistor [resistance=100 tolerance=±5% package=THT]
  R2 = Resistor [resistance=100 tolerance=±5% package=THT]
  LED1 = RGB LED - (4 legs) [package="5 mm [THT]"]

nets:
  N1: RGB_Shield.D11, R1.Pin_0
  N2: RGB_Shield.D10, R2.Pin_0
  N3: RGB_Shield.D9, R3.Pin_0
  N4: RGB_Shield.+5V, LED1.common_anode
  N5: R1.Pin_1, LED1.red_cathode
  N6: R3.Pin_1, LED1.blue_cathode
  N7: R2.Pin_1, LED1.green_cathode

notes:
  Let the light shine in any color!
  Check out this forum post for a good code example.

// code stored in the sketch: ___lockfile___.txt

