# Fritzing sketch Sabotage-Detection (saved by Fritzing 0.6.4b)
breadboards: 1

parts:
  Arduino1 = Arduino
  S1 = Pushbutton [package="[THT]"]
  R1 = Resistor [tolerance=±5% resistance=220 package=THT]
  R2 = Resistor [tolerance=±5% resistance=220 package=THT]
  R3 = Resistor [tolerance=±5% resistance=1.1k package=THT]
  R4 = Resistor [tolerance=±5% resistance=220 package=THT]
  LED3 = LED - 5mm [color="Green (555nm)" package="5 mm [THT]"]
  R5 = Rotary Potentiometer (Small) [maximum_resistance=10kΩ]
  LED5 = led_flux_blue_cathode [color=Blue]
  Bauteil1 = Triple Axis Accelerometer Breakout - ADXL335
  LED6 = led_flux_blue_cathode [color=Blue]

nets (from the pcb view):
  GND: Arduino1.GND, R1.Pin_0, R2.Pin_0, R3.Pin_0, R4.Pin_0, R5.leg2, Bauteil1.GND
  N1: Arduino1.D11, LED3.anode
  N2: Arduino1.D7, LED6.connector0
  N3: Arduino1.D3, LED5.connector0
  N4: Arduino1.D2, S1.Pin_3, S1.Pin_4, R3.Pin_1
  3V3: Arduino1.3V3, Bauteil1.VCC
  N5: Arduino1.+5V, S1.Pin_1, S1.Pin_2, R5.leg1
  N6: Arduino1.A0, Bauteil1.ZOUT
  N7: Arduino1.A1, Bauteil1.YOUT
  N8: Arduino1.A2, Bauteil1.XOUT
  N9: Arduino1.A3, R5.wiper
  N10: R1.Pin_1, LED6.connector2
  N11: R2.Pin_1, LED5.connector1
  N12: R4.Pin_1, LED3.cathode

notes:
  Get the Arduino Code from here:
  Sabotage Alert
