# Fritzing sketch Shift_Register (saved by Fritzing 0.3.7b)
breadboards: 2

parts:
  74HC5951 = 74HC595 [package="DIP16 [THT]"]
  Arduino1 = Arduino
  C1 = Ceramic Capacitor [package=THT]
  R1 = 220 Ω Resistor [package=THT]
  R1_2 = 220 Ω Resistor [package=THT]
  R1_3 = 220 Ω Resistor [package=THT]
  R1_4 = 220 Ω Resistor [package=THT]
  R1_5 = 220 Ω Resistor [package=THT]
  R1_6 = 220 Ω Resistor [package=THT]
  R1_7 = 220 Ω Resistor [package=THT]
  R1_8 = 220 Ω Resistor [package=THT]
  LED1 = Red LED - 5mm
  LED1_2 = Red LED - 5mm
  LED1_3 = Red LED - 5mm
  LED1_4 = Red LED - 5mm
  LED1_5 = Red LED - 5mm
  LED1_6 = Red LED - 5mm
  LED1_7 = Red LED - 5mm
  LED1_8 = Red LED - 5mm

nets:
  N1: 74HC5951.Q1, R1_2.Pin_1
  N2: 74HC5951.Q2, R1_3.Pin_1
  N3: 74HC5951.Q3, R1_4.Pin_1
  N4: 74HC5951.Q4, R1_6.Pin_1
  N5: 74HC5951.Q5, R1_7.Pin_1
  N6: 74HC5951.Q6, R1_8.Pin_1
  N7: 74HC5951.Q7, R1_5.Pin_1
  GND: 74HC5951.GND, 74HC5951.OE, Arduino1.GND, C1.pin_1, LED1.cathode, LED1_2.cathode, LED1_3.cathode, LED1_4.cathode, LED1_5.cathode, LED1_6.cathode, LED1_7.cathode, LED1_8.cathode
  VCC: 74HC5951.MR, 74HC5951.VCC, Arduino1.+5V
  N8: 74HC5951.SH_CP, Arduino1.D12
  N9: 74HC5951.ST_CP, Arduino1.D8, C1.pin_0
  N10: 74HC5951.DS, Arduino1.D11
  N11: 74HC5951.Q0, R1.Pin_1
  N12: R1.Pin_0, LED1.anode
  N13: R1_2.Pin_0, LED1_2.anode
  N14: R1_3.Pin_0, LED1_3.anode
  N15: R1_4.Pin_0, LED1_5.anode
  N16: R1_5.Pin_0, LED1_7.anode
  N17: R1_6.Pin_0, LED1_6.anode
  N18: R1_7.Pin_0, LED1_8.anode
  N19: R1_8.Pin_0, LED1_4.anode

notes:
  In this project, a 74HC595 shift register is used to control 8 LEDs with just 3 Arduino pins.
  Related example: http://www.arduino.cc/en/Tutorial/ShiftOut
