# Fritzing sketch Shift_Register_2x (saved by Fritzing 0.7.0b)
breadboards: 1

parts:
  Arduino1 = Arduino
  LED1 = LED - 5mm [color="Red (633nm)" package="5 mm [THT]"]
  LED2 = LED - 5mm [color="Red (633nm)" package="5 mm [THT]"]
  LED3 = LED - 5mm [color="Red (633nm)" package="5 mm [THT]"]
  LED4 = LED - 5mm [color="Red (633nm)" package="5 mm [THT]"]
  LED7 = LED - 5mm [color="Red (633nm)" package="5 mm [THT]"]
  LED5 = LED - 5mm [color="Red (633nm)" package="5 mm [THT]"]
  LED6 = LED - 5mm [color="Red (633nm)" package="5 mm [THT]"]
  LED8 = LED - 5mm [color="Red (633nm)" package="5 mm [THT]"]
  LED15 = LED - 5mm [color="Red (633nm)" package="5 mm [THT]"]
  LED14 = LED - 5mm [color="Red (633nm)" package="5 mm [THT]"]
  LED11 = LED - 5mm [color="Red (633nm)" package="5 mm [THT]"]
  LED16 = LED - 5mm [color="Red (633nm)" package="5 mm [THT]"]
  LED9 = LED - 5mm [color="Red (633nm)" package="5 mm [THT]"]
  LED13 = LED - 5mm [color="Red (633nm)" package="5 mm [THT]"]
  LED12 = LED - 5mm [color="Red (633nm)" package="5 mm [THT]"]
  LED10 = LED - 5mm [color="Red (633nm)" package="5 mm [THT]"]
  R1 = Resistor [tolerance=±5% resistance=220 package=THT]
  R2 = Resistor [tolerance=±5% resistance=220 package=THT]
  R3 = Resistor [tolerance=±5% resistance=220 package=THT]
  R4 = Resistor [tolerance=±5% resistance=220 package=THT]
  R5 = Resistor [tolerance=±5% resistance=220 package=THT]
  R6 = Resistor [tolerance=±5% resistance=220 package=THT]
  R7 = Resistor [tolerance=±5% resistance=220 package=THT]
  R8 = Resistor [tolerance=±5% resistance=220 package=THT]
  R9 = Resistor [tolerance=±5% resistance=220 package=THT]
  R10 = Resistor [tolerance=±5% resistance=220 package=THT]
  R11 = Resistor [tolerance=±5% resistance=220 package=THT]
  R12 = Resistor [tolerance=±5% resistance=220 package=THT]
  R13 = Resistor [tolerance=±5% resistance=220 package=THT]
  R14 = Resistor [tolerance=±5% resistance=220 package=THT]
  R15 = Resistor [tolerance=±5% resistance=220 package=THT]
  R16 = Resistor [tolerance=±5% resistance=220 package=THT]
  U1 = 74HC595 [package="DIP16 [THT]"]
  U2 = 74HC595 [package="DIP16 [THT]"]
  C1 = Ceramic Capacitor [capacitance=100nF package="100 mil [THT, multilayer]"]

nets:
  GND: Arduino1.GND, R1.Pin_0, R2.Pin_0, R3.Pin_0, R4.Pin_0, R5.Pin_0, R6.Pin_0, R7.Pin_0, R8.Pin_0, R9.Pin_0, R10.Pin_0, R11.Pin_0, R12.Pin_0, R13.Pin_0, R14.Pin_0, R15.Pin_0, R16.Pin_0, U1.GND, U1.OE, U2.GND, U2.OE, C1.1
  N1: Arduino1.D12, U1.SH_CP, U2.SH_CP
  N2: Arduino1.D11, U1.DS
  N3: Arduino1.D8, U1.ST_CP, U2.ST_CP, C1.0
  VCC: Arduino1.+5V, U1.MR, U1.VCC, U2.MR, U2.VCC
  N4: LED1.cathode, R1.Pin_1
  N5: LED1.anode, U2.Q7
  N6: LED2.cathode, R2.Pin_1
  N7: LED2.anode, U2.Q6
  N8: LED3.cathode, R3.Pin_1
  N9: LED3.anode, U2.Q5
  N10: LED4.cathode, R4.Pin_1
  N11: LED4.anode, U2.Q4
  N12: LED7.cathode, R6.Pin_1
  N13: LED7.anode, U2.Q1
  N14: LED5.cathode, R5.Pin_1
  N15: LED5.anode, U2.Q3
  N16: LED6.cathode, R8.Pin_1
  N17: LED6.anode, U2.Q2
  N18: LED8.cathode, R7.Pin_1
  N19: LED8.anode, U2.Q0
  N20: LED15.cathode, R14.Pin_1
  N21: LED15.anode, U1.Q1
  N22: LED14.cathode, R16.Pin_1
  N23: LED14.anode, U1.Q2
  N24: LED11.cathode, R10.Pin_1
  N25: LED11.anode, U1.Q5
  N26: LED16.cathode, R15.Pin_1
  N27: LED16.anode, U1.Q0
  N28: LED9.cathode, R9.Pin_1
  N29: LED9.anode, U1.Q7
  N30: LED13.cathode, R13.Pin_1
  N31: LED13.anode, U1.Q3
  N32: LED12.cathode, R11.Pin_1
  N33: LED12.anode, U1.Q4
  N34: LED10.cathode, R12.Pin_1
  N35: LED10.anode, U1.Q6
  N36: U1.Q7', U2.DS

notes:
  In this project, two 74HC595 shift register are used to control 16 LEDs with just 3 Arduino pins.
  Related example: http://www.arduino.cc/en/Tutorial/ShiftOut

// code stored in the sketch: ___lockfile___.txt

