# Fritzing sketch Stepper_Motor (saved by Fritzing 0.7.0b)
breadboards: 1

parts:
  Q4 = NPN-Transistor [package="TO92 [THT]"]
  Q3 = NPN-Transistor [package="TO92 [THT]"]
  IC1 = H-Bridge [package=THT]
  Power_plug1 = Power plug
  R13 = Resistor [resistance=1k tolerance=±5% package=THT]
  R10 = Resistor [resistance=1k tolerance=±5% package=THT]
  R12 = Resistor [resistance=10k tolerance=±5% package=THT]
  R11 = Resistor [resistance=10k tolerance=±5% package=THT]
  Arduino1 = Arduino
  M1 = Stepper Motor - Bipolar

nets:
  GND: Q4.E, Q3.E, IC1.GND1, IC1.GND2, IC1.GND3, IC1.GND4, Power_plug1.GND, Arduino1.GND
  N1: Q4.B, R13.Pin_0
  N2: Q4.C, IC1.3A, R12.Pin_0
  N3: Q3.B, R10.Pin_0
  N4: Q3.C, IC1.2A, R11.Pin_1
  N5: IC1.1_2EN, IC1.3_4EN, IC1.VCC1, R12.Pin_1, R11.Pin_0, Arduino1.+5V
  N6: IC1.1A, R10.Pin_1, Arduino1.D10
  N7: IC1.1Y, M1.A
  N8: IC1.2Y, M1.C
  N9: IC1.VCC2, Power_plug1.VCC
  N10: IC1.3Y, M1.D
  N11: IC1.4Y, M1.B
  N12: IC1.4A, R13.Pin_1, Arduino1.D11

notes:
  This project shows how to control a stepper motor's direction (running forwards and backwards) using an H-bridge. An H-bridge is an electronic circuit which enables a voltage to be applied across a load in either direction.
  Related Examples: Stepper Motor Control

// code stored in the sketch: ___lockfile___.txt

