# Fritzing sketch TemperaturSensorLM35 (saved by Fritzing 0.6.4b)
breadboards: 1

parts:
  Arduino1 = Arduino
  T1 = LM35 Temperature Sensor [package="TO92 [THT]"]
  R1 = Resistor [tolerance=±5% resistance=220 package=THT]
  LED1 = LED - 5mm [color="Green (555nm)" package="5 mm [THT]"]
  R2 = Resistor [tolerance=±5% resistance=220 package=THT]
  R3 = Resistor [tolerance=±5% resistance=220 package=THT]
  R4 = Resistor [tolerance=±5% resistance=220 package=THT]
  R5 = Resistor [tolerance=±5% resistance=220 package=THT]
  R6 = Resistor [tolerance=±5% resistance=220 package=THT]
  R7 = Resistor [tolerance=±5% resistance=220 package=THT]
  R8 = Resistor [tolerance=±5% resistance=220 package=THT]
  LED2 = LED - 5mm [color="Green (555nm)" package="5 mm [THT]"]
  LED3 = LED - 5mm [color="Green (555nm)" package="5 mm [THT]"]
  LED4 = LED - 5mm [color="Green (555nm)" package="5 mm [THT]"]
  LED5 = LED - 5mm [color="Green (555nm)" package="5 mm [THT]"]
  LED6 = LED - 5mm [color="Yellow (595nm)" package="5 mm [THT]"]
  LED7 = LED - 5mm [color="Red (633nm)" package="5 mm [THT]"]
  LED8 = LED - 5mm [color="Red (633nm)" package="5 mm [THT]"]
  LED9 = LED - 5mm [color="Red (633nm)" package="5 mm [THT]"]
  LED10 = LED - 5mm [color="Red (633nm)" package="5 mm [THT]"]
  LED11 = LED - 5mm [color="Red (633nm)" package="5 mm [THT]"]
  R9 = Resistor [tolerance=±5% resistance=220 package=THT]
  R10 = Resistor [tolerance=±5% resistance=220 package=THT]
  R11 = Resistor [tolerance=±5% resistance=220 package=THT]

nets:
  N1: Arduino1.D12, LED11.cathode
  N2: Arduino1.D11, LED10.cathode
  N3: Arduino1.D10, LED9.cathode
  N4: Arduino1.D9, LED8.cathode
  N5: Arduino1.D8, LED7.cathode
  N6: Arduino1.D7, LED6.cathode
  N7: Arduino1.D6, LED5.cathode
  N8: Arduino1.D5, LED4.cathode
  N9: Arduino1.D4, LED3.cathode
  N10: Arduino1.D3, LED2.cathode
  N11: Arduino1.D2, LED1.cathode
  N12: Arduino1.+5V, T1.+Vs
  GND: Arduino1.GND, T1.GND, R1.Pin_0, R2.Pin_0, R3.Pin_0, R4.Pin_0, R5.Pin_0, R6.Pin_0, R7.Pin_0, R8.Pin_0, R9.Pin_0, R10.Pin_0, R11.Pin_0
  N13: Arduino1.A0, T1.Vout
  N14: R1.Pin_1, LED1.anode
  N15: R2.Pin_1, LED2.anode
  N16: R3.Pin_1, LED3.anode
  N17: R4.Pin_1, LED4.anode
  N18: R5.Pin_1, LED5.anode
  N19: R6.Pin_1, LED6.anode
  N20: R7.Pin_1, LED11.anode
  N21: R8.Pin_1, LED8.anode
  N22: LED7.anode, R11.Pin_1
  N23: LED9.anode, R9.Pin_1
  N24: LED10.anode, R10.Pin_1

notes:
  Digital Thermometer
  get the code from here
  Digital Thermometer with LM35
