# Fritzing sketch TemperaturSensorLM35 (saved by Fritzing 0.7.0b)
breadboards: 1

parts:
  Arduino1 = Arduino
  T1 = LM35 Temperature Sensor [package="TO92 [THT]"]
  R1 = Resistor [tolerance=±5% resistance=220 package=THT]
  LED1 = LED - 5mm [color="Green (555nm)" package="5 mm [THT]"]
  R2 = Resistor [tolerance=±5% resistance=220 package=THT]
  R3 = Resistor [tolerance=±5% resistance=220 package=THT]
  R4 = Resistor [tolerance=±5% resistance=220 package=THT]
  R5 = Resistor [tolerance=±5% resistance=220 package=THT]
  R6 = Resistor [tolerance=±5% resistance=220 package=THT]
  LED2 = LED - 5mm [color="Green (555nm)" package="5 mm [THT]"]
  LED3 = LED - 5mm [color="Yellow (595nm)" package="5 mm [THT]"]
  LED4 = LED - 5mm [color="Yellow (595nm)" package="5 mm [THT]"]
  LED5 = LED - 5mm [color="Red (633nm)" package="5 mm [THT]"]
  LED6 = LED - 5mm [color="Red (633nm)" package="5 mm [THT]"]

nets:
  GND: Arduino1.GND, T1.GND, R1.Pin_0, R2.Pin_0, R3.Pin_0, R4.Pin_0, R5.Pin_0, R6.Pin_0
  N1: Arduino1.D7, LED6.cathode
  N2: Arduino1.D6, LED5.cathode
  N3: Arduino1.D5, LED4.cathode
  N4: Arduino1.D4, LED3.cathode
  N5: Arduino1.D3, LED2.cathode
  N6: Arduino1.D2, LED1.cathode
  N7: Arduino1.+5V, T1.+Vs
  N8: Arduino1.A0, T1.Vout
  N9: R1.Pin_1, LED1.anode
  N10: R2.Pin_1, LED2.anode
  N11: R3.Pin_1, LED3.anode
  N12: R4.Pin_1, LED4.anode
  N13: R5.Pin_1, LED5.anode
  N14: R6.Pin_1, LED6.anode

notes:
  Digital Thermometer
  get the code from here
  Digital Thermometer with LM35

// code stored in the sketch: ___lockfile___.txt

