# Fritzing sketch TiltSwitch (saved by Fritzing 0.3.9b)
breadboards: 1

parts:
  LED1 = Red LED - 5mm
  S1 = Tilt Switch [package=THT]
  Arduino1 = Arduino
  R2 = Resistor [resistance=10k package=THT]

nets:
  N1: LED1.cathode, Arduino1.GND, R2.Pin_1
  N2: LED1.anode, Arduino1.D13
  N3: S1.Pin_1, Arduino1.+5V
  N4: S1.Pin_2, Arduino1.D2, R2.Pin_0

notes:
  In this example, a tilt switch is used (just like a button) as a digital input, and an LED is a digital output. The resistor is a pull-down resistor.
  Related example: http://www.arduino.cc/en/Tutorial/TiltSensor
