# Fritzing sketch TiltSwitch (saved by Fritzing 0.7.0b)
breadboards: 1

parts:
  S1 = Tilt Switch [package=THT]
  Arduino1 = Arduino
  R2 = Resistor [resistance=10k tolerance=±5% package=THT]
  LED2 = LED - 5mm [color="Red (633nm)" package="5 mm [THT]"]

nets:
  N1: S1.Pin_1, Arduino1.+5V
  N2: S1.Pin_2, Arduino1.D2, R2.Pin_0
  N3: Arduino1.GND, R2.Pin_1, LED2.cathode
  N4: Arduino1.D13, LED2.anode

notes:
  In this example, a tilt switch is used (just like a button) as a digital input, and an LED is a digital output. The resistor is a pull-down resistor.
  Related example: http://www.arduino.cc/en/Tutorial/TiltSensor

// code stored in the sketch: ___lockfile___.txt

