# Fritzing sketch Timer (saved by Fritzing 0.7.0b)
breadboards: 1

parts:
  DI1 = 7-Segment LED Display [package=THT]
  DI2 = 7-Segment LED Display [package=THT]
  U1 = 74HC595 [package="DIP16 [THT]"]
  U2 = 74HC595 [package="DIP16 [THT]"]
  R1 = Resistor [resistance=220 tolerance=±5% package=THT]
  R1_2 = Resistor [resistance=220 tolerance=±5% package=THT]
  R1_3 = Resistor [resistance=220 tolerance=±5% package=THT]
  R1_4 = Resistor [resistance=220 tolerance=±5% package=THT]
  R1_5 = Resistor [resistance=220 tolerance=±5% package=THT]
  R1_6 = Resistor [resistance=220 tolerance=±5% package=THT]
  R1_7 = Resistor [resistance=220 tolerance=±5% package=THT]
  R1_8 = Resistor [resistance=220 tolerance=±5% package=THT]
  R1_9 = Resistor [resistance=220 tolerance=±5% package=THT]
  R1_10 = Resistor [resistance=220 tolerance=±5% package=THT]
  R1_11 = Resistor [resistance=220 tolerance=±5% package=THT]
  R1_12 = Resistor [resistance=220 tolerance=±5% package=THT]
  R1_13 = Resistor [resistance=220 tolerance=±5% package=THT]
  R1_14 = Resistor [resistance=220 tolerance=±5% package=THT]
  S1 = Pushbutton [package="[THT]"]
  S1_2 = Pushbutton [package="[THT]"]
  R3 = Resistor [resistance=10k tolerance=±5% package=THT]
  R3_2 = Resistor [resistance=10k tolerance=±5% package=THT]
  Arduino1 = Arduino

nets:
  N1: DI1.cathodeE, R1_5.Pin_0
  N2: DI1.cathodeD, R1_4.Pin_0
  VCC: DI1.commAnode, DI2.commAnode#7, U1.MR, U1.VCC, U2.MR, U2.VCC, S1.Pin_3, S1.Pin_4, S1_2.Pin_3, S1_2.Pin_4, Arduino1.+5V
  N3: DI1.cathodeC, R1_3.Pin_0
  N4: DI1.cathodeB, R1_2.Pin_0
  N5: DI1.cathodeA, R1.Pin_1
  N6: DI1.cathodeF, R1_6.Pin_0
  N7: DI1.cathodeG, R1_7.Pin_0
  N8: DI2.cathodeE, R1_12.Pin_0
  N9: DI2.cathodeD, R1_11.Pin_0
  N10: DI2.cathodeC, R1_10.Pin_0
  N11: DI2.cathodeB, R1_9.Pin_0
  N12: DI2.cathodeA, R1_8.Pin_1
  N13: DI2.cathodeF, R1_13.Pin_0
  N14: DI2.cathodeG, R1_14.Pin_0
  N15: U1.Q1, R1_2.Pin_1
  N16: U1.Q2, R1_3.Pin_1
  N17: U1.Q3, R1_4.Pin_1
  N18: U1.Q4, R1_5.Pin_1
  N19: U1.Q5, R1_6.Pin_1
  N20: U1.Q6, R1_7.Pin_1
  GND: U1.GND, U1.OE, U2.GND, U2.OE, R3.Pin_1, R3_2.Pin_1, Arduino1.GND
  N21: U1.SH_CP, U2.SH_CP, Arduino1.D12
  N22: U1.ST_CP, U2.ST_CP, Arduino1.D8
  N23: U1.DS, U2.Q7'
  N24: U1.Q0, R1.Pin_0
  N25: U2.Q1, R1_9.Pin_1
  N26: U2.Q2, R1_10.Pin_1
  N27: U2.Q3, R1_11.Pin_1
  N28: U2.Q4, R1_12.Pin_1
  N29: U2.Q5, R1_13.Pin_1
  N30: U2.Q6, R1_14.Pin_1
  N31: U2.DS, Arduino1.D11
  N32: U2.Q0, R1_8.Pin_0
  N33: S1.Pin_1, S1.Pin_2, R3_2.Pin_0, Arduino1.D6
  N34: S1_2.Pin_1, S1_2.Pin_2, R3.Pin_0, Arduino1.D5

notes:
  Example from Frerk Popovic
  www.popovic.info
