# Fritzing sketch TouchSwitch (saved by Fritzing 0.3.9b)
breadboards: 1

parts:
  Q1 = NPN-Transistor [package="TO92 [THT]"]
  Q1_2 = NPN-Transistor [package="TO92 [THT]"]
  Arduino1 = Arduino
  LED1 = Red LED - 5mm
  R5 = Resistor [resistance=10k package=THT]
  R6 = Resistor [resistance=1k package=THT]
  R7 = Resistor [resistance=10k package=THT]
  ANT1 = Antenna
  ANT2 = Antenna

nets:
  N1: Q1.emitter, R6.Pin_0
  N2: Q1.base, ANT2.antenna_lead
  N3: Q1.collector, R5.Pin_0
  N4: Q1_2.emitter, Arduino1.A0, R7.Pin_0
  N5: Q1_2.base, R5.Pin_1
  N6: Q1_2.collector, Arduino1.GND, LED1.cathode
  N7: Arduino1.D13, LED1.anode
  N8: Arduino1.+5V, R6.Pin_1, R7.Pin_1, ANT1.antenna_lead

notes:
  A simple touch switch can be created by using two NPN transistors. When touching the two blue cables, the LED will turn on. (download code from the project page)
  http://en.wikipedia.org/wiki/Darlington_transistor
