# Fritzing sketch TouchSwitch (saved by Fritzing 0.7.0b)
breadboards: 1

parts:
  Arduino1 = Arduino
  R5 = Resistor [resistance=10k tolerance=±5% package=THT]
  R6 = Resistor [resistance=1k tolerance=±5% package=THT]
  R7 = Resistor [resistance=10k tolerance=±5% package=THT]
  TOUCH_IT! = Antenna
  ANT2 = Antenna
  Q2 = NPN-Transistor [package="TO92 [THT]"]
  Q3 = NPN-Transistor [package="TO92 [THT]"]
  LED2 = LED - 5mm [color="Red (633nm)" package="5 mm [THT]"]

nets:
  N1: Arduino1.GND, Q2.C, LED2.cathode
  N2: Arduino1.D13, LED2.anode
  N3: Arduino1.+5V, R6.Pin_1, R7.Pin_1, TOUCH_IT!.antenna_lead
  N4: Arduino1.A0, R7.Pin_0, Q2.E
  N5: R5.Pin_0, Q3.C
  N6: R5.Pin_1, Q2.B
  N7: R6.Pin_0, Q3.E
  N8: ANT2.antenna_lead, Q3.B

notes:
  A simple touch switch can be created by using two NPN transistors. When touching the two blue cables, the LED will turn on. (download code from the project page)
  http://en.wikipedia.org/wiki/Darlington_transistor

// code stored in the sketch: ___lockfile___.txt

