# Fritzing sketch TrafficLight (saved by Fritzing 0.2.2)
breadboards: 1

parts:
  Arduino1 = Arduino Diecimila (deprecated) [package=THT]
  LED1 = Red LED - 5mm
  R1 = 220 Ω Resistor [package=THT]
  LED2 = yellow LED - 5mm
  R2 = 220 Ω Resistor [package=THT]
  LED3 = green LED - 5mm
  R3 = 220 Ω Resistor [package=THT]
  S1 = Pushbutton [package=THT]
  R4 = 220 Ω Resistor [package=THT]
  LED4 = Red LED - 5mm
  LED5 = green LED - 5mm
  R5 = 220 Ω Resistor [package=THT]
  R6 = 220 Ω Resistor [package=THT]

nets:
  N1: Arduino1.GND, LED1.cathode, LED2.cathode, LED3.cathode, R4.Pin_0, LED4.cathode, LED5.cathode
  N2: Arduino1.D12, R1.Pin_1
  N3: Arduino1.D11, R2.Pin_1
  N4: Arduino1.D10, R3.Pin_1
  N5: Arduino1.D9, R6.Pin_1
  N6: Arduino1.D8, R5.Pin_1
  N7: Arduino1.D2, S1.leg1, R4.Pin_1
  N8: Arduino1.+5V, S1.leg0
  N9: LED1.anode, R1.Pin_0
  N10: LED2.anode, R2.Pin_0
  N11: LED3.anode, R3.Pin_0
  N12: LED4.anode, R5.Pin_0
  N13: LED5.anode, R6.Pin_0

notes:
  This circuit can be coded such that both the car and pedestrian traffic lights go through their normal cycle until the button is pressed by a pedestrian. In this case, the lights will change in favor of the pedestrian.
  Car Traffic Light
  Pedestrian Traffic Light
