# Fritzing sketch TrafficLight (saved by Fritzing 0.7.0b)
breadboards: 1

parts:
  Arduino2 = Arduino
  R7 = Resistor [resistance=220 tolerance=±5% package=THT]
  S2 = Pushbutton [package=THT]
  R8 = Resistor [resistance=220 tolerance=±5% package=THT]
  R9 = Resistor [resistance=220 tolerance=±5% package=THT]
  R10 = Resistor [resistance=220 tolerance=±5% package=THT]
  R11 = Resistor [resistance=220 tolerance=±5% package=THT]
  R12 = Resistor [resistance=220 tolerance=±5% package=THT]
  LED8 = LED - 5mm [color="Green (555nm)" package="5 mm [THT]"]
  LED10 = LED - 5mm [color="Red (633nm)" package="5 mm [THT]"]
  LED7 = LED - 5mm [color="Yellow (585nm)" package="5 mm [THT]"]
  LED6 = LED - 5mm [color="Green (555nm)" package="5 mm [THT]"]
  LED9 = LED - 5mm [color="Red (633nm)" package="5 mm [THT]"]

nets:
  N1: Arduino2.GND, R11.Pin_0, LED8.cathode, LED10.cathode, LED7.cathode, LED6.cathode, LED9.cathode
  N2: Arduino2.D12, R7.Pin_1
  N3: Arduino2.D11, R9.Pin_1
  N4: Arduino2.D10, R10.Pin_1
  N5: Arduino2.D9, R8.Pin_1
  N6: Arduino2.D8, R12.Pin_1
  N7: Arduino2.D2, S2.leg1, R11.Pin_1
  N8: Arduino2.+5V, S2.leg0
  N9: R7.Pin_0, LED10.anode
  N10: R8.Pin_0, LED6.anode
  N11: R9.Pin_0, LED7.anode
  N12: R10.Pin_0, LED8.anode
  N13: R12.Pin_0, LED9.anode

notes:
  This circuit can be coded such that both the car and pedestrian traffic lights go through their normal cycle until the button is pressed by a pedestrian. In this case, the lights will change in favor of the pedestrian.
  Car Traffic Light
  Pedestrian Traffic Light

// code stored in the sketch: ___lockfile___.txt

