# Fritzing sketch VirtualColorMixer (saved by Fritzing 0.7.0b)
breadboards: 1

parts:
  Arduino1 = Arduino
  R1 = Rotary Potentiometer (Large) [maximum_resistance=100kΩ package=THT]
  R1_2 = Rotary Potentiometer (Large) [maximum_resistance=100kΩ package=THT]
  R1_3 = Rotary Potentiometer (Large) [maximum_resistance=100kΩ package=THT]

nets:
  N1: Arduino1.GND, R1.leg2, R1_2.leg2, R1_3.leg2
  N2: Arduino1.+5V, R1.leg1, R1_2.leg1, R1_3.leg1
  N3: Arduino1.A0, R1_2.wiper
  N4: Arduino1.A1, R1_3.wiper
  N5: Arduino1.A2, R1.wiper

notes:
  You can send multiple values from the Arduino board to the computer using the serial print function. In this project, the analog values from three potentiometers are used to set the red, green, and blue values of the background color of a Processing sketch running on the computer.
  http://arduino.cc/en/Tutorial/VirtualColorMixer

// code stored in the sketch: ___lockfile___.txt

