# Fritzing sketch VirtualColorMixer_double_sided (saved by Fritzing 0.3.21b)
breadboards: 1

parts:
  R1 = Rotary Potentiometer (Large) [package=THT]
  R1_2 = Rotary Potentiometer (Large) [package=THT]
  R1_3 = Rotary Potentiometer (Large) [package=THT]
  Arduino1 = Arduino

nets:
  N1: R1.leg1, R1_2.leg1, R1_3.leg1, Arduino1.+5V
  N2: R1.wiper, Arduino1.A0
  N3: R1.leg2, R1_2.leg2, R1_3.leg2, Arduino1.GND
  N4: R1_2.wiper, Arduino1.A1
  N5: R1_3.wiper, Arduino1.A2

notes:
  You can send multiple values from the Arduino board to the computer using the serial print function. In this project, the analog values from three potentiometers are used to set the red, green, and blue values of the background color of a Processing sketch running on the computer.
  http://arduino.cc/en/Tutorial/VirtualColorMixer
