# Fritzing sketch VoltageRegulator_7800series (saved by Fritzing 0.7.0b)
breadboards: 1

parts:
  U1 = Voltage Regulator - 5V [package="TO220 [THT]"]
  Power_plug1 = Power plug
  J3 = female pin header, 2 pins [form="♂ (male)"]
  C2 = Electrolytic Capacitor [capacitance=100nF rated_voltage=35V package="100 mil [THT, electrolytic]"]
  C1 = Electrolytic Capacitor [capacitance=100nF rated_voltage=35V package="100 mil [THT, electrolytic]"]

nets:
  N1: U1.input_voltage, Power_plug1.VCC, C1.+
  GND: U1.GND, Power_plug1.GND, J3.pin2, C2.-, C1.-
  N2: U1.output_voltage, J3.pin1, C2.+

notes:
  This example uses a 7805 voltage regulator to regulate voltage to 5 volts. The input should be at least 7V DC.

// code stored in the sketch: ___lockfile___.txt

