# Fritzing sketch VoltageRegulator_with_switch (saved by Fritzing 0.7.0b)
breadboards: 1

parts:
  S1 = Toggle Switch [package=THT]
  U1 = Voltage Regulator - 5V [package="TO220 [THT]"]
  Power_plug1 = Power plug
  J3 = female pin header, 2 pins [form="♂ (male)"]
  C2 = Electrolytic Capacitor [capacitance=100nF rated_voltage=35V package="100 mil [THT, electrolytic]"]
  C1 = Electrolytic Capacitor [capacitance=100nF rated_voltage=35V package="100 mil [THT, electrolytic]"]

nets:
  N1: S1.COM, U1.input_voltage, C1.+
  N2: S1.L2, Power_plug1.VCC
  GND: U1.GND, Power_plug1.GND, J3.pin2, C2.-, C1.-
  N3: U1.output_voltage, J3.pin1, C2.+

notes:
  This example uses a 7805 voltage regulator to regulate voltage to 5 volts. There is a switch to turn power to the circuit on and off. The battery should be at least 7V DC.

// code stored in the sketch: ___lockfile___.txt

