# Fritzing sketch Window_Alarm (saved by Fritzing 0.3.4b)
breadboards: 1

parts:
  S1 = Reed switch [package=THT]
  R1 = 10k Ω Resistor [package=THT]
  J1 = Piezo Speaker
  Arduino2 = Arduino

nets:
  N1: S1.pin_1, R1.Pin_0, Arduino2.D12
  N2: S1.pin_2, Arduino2.+5V
  N3: R1.Pin_1, J1.pin1, Arduino2.GND
  N4: J1.pin2, Arduino2.D9

notes:
  Reed switches close when a magnet is placed near their casing. In this example, a magnet could be mounted on a window and the reed switch on the windowsill so that everytime the window was opened, the piezo buzzer would sound.
  http://arduino.cc/en/Tutorial/Button
  http://arduino.cc/en/Tutorial/Melody
