# Fritzing sketch Window_Alarm (saved by Fritzing 0.7.0b)
breadboards: 1

parts:
  J1 = Piezo Speaker
  Arduino2 = Arduino
  R2 = Resistor [resistance=10k tolerance=±5% package=THT]
  S2 = Reed switch [package=THT]

nets:
  N1: J1.pin1, Arduino2.GND, R2.Pin_1
  N2: J1.pin2, Arduino2.D9
  N3: Arduino2.D12, R2.Pin_0, S2.pin_1
  N4: Arduino2.+5V, S2.pin_2

notes:
  Reed switches close when a magnet is placed near their casing. In this example, a magnet could be mounted on a window and the reed switch on the windowsill so that everytime the window was opened, the piezo buzzer would sound.
  http://arduino.cc/en/Tutorial/Button
  http://arduino.cc/en/Tutorial/Melody

// code stored in the sketch: ___lockfile___.txt

