# Fritzing sketch color-fader (saved by Fritzing 0.7.0b)
breadboards: 1

parts:
  LED1 = RGB LED (com. cathode, rbg) [package="5 mm [THT]"]
  R1 = Resistor [tolerance=±5% resistance=220 package=THT]
  R3 = Resistor [tolerance=±5% resistance=220 package=THT]
  R2 = Resistor [tolerance=±5% resistance=220 package=THT]
  R4 = Rotary Potentiometer (Small) [maximum_resistance=100kΩ]
  Arduino1 = Arduino

nets:
  N1: LED1.red_anode, R1.Pin_1
  N2: LED1.common_cathode, R4.leg1, Arduino1.GND
  N3: LED1.blue_anode, R3.Pin_1
  N4: LED1.green_anode, R2.Pin_1
  N5: R1.Pin_0, Arduino1.D11
  N6: R3.Pin_0, Arduino1.D10
  N7: R2.Pin_0, Arduino1.D9
  N8: R4.wiper, Arduino1.A0
  N9: R4.leg2, Arduino1.+5V

notes:
  A potentiometer is used to display rainbow colors on an rgb LED. It is the type in the Fritzing Starter Kits (pins: red, com. cathode, blue, green).
  Get the Arduino-Code from here:
  http://fritzing.org/projects/color-fader/

// code stored in the sketch: color-Fader.ino
/*
  _____       .__  __         .__                
_/ ____\______|__|/  |________|__| ____    ____  
\   __\\_  __ \  \   __\___   /  |/    \  / ___\ 
 |  |   |  | \/  ||  |  /    /|  |   |  \/ /_/  >
 |__|   |__|  |__||__| /_____ \__|___|  /\___  / 
                             \/       \//_____/  
          __                 __                  __   .__  __   
  _______/  |______ ________/  |_  ___________  |  | _|__|/  |_ 
 /  ___/\   __\__  \\_  __ \   __\/ __ \_  __ \ |  |/ /  \   __\
 \___ \  |  |  / __ \|  | \/|  | \  ___/|  | \/ |    <|  ||  |  
/____  > |__| (____  /__|   |__|  \___  >__|    |__|_ \__||__|  
     \/            \/                 \/             \/         

Example      RGB LED Fader
Autor        Stefan Hermann
Date         16.06.2011

Description  This example lets you fade through the colors of a RGB LED.

*/

int LEDGreen=9;
int LEDBlue=10;
int LEDRed=11;


int sensorPin=0;
int val;

void setup(){
  Serial.begin(9600);
  pinMode(LEDRed,OUTPUT);
  pinMode(LEDGreen,OUTPUT);
  pinMode(LEDBlue,OUTPUT);  
}

void loop(){
  
  val=map(analogRead(sensorPin),0,1024,0,900);
  Serial.println(val);
  if (val<150) {
    analogWrite(LEDRed,0);
    analogWrite(LEDBlue,255); 
    analogWrite(LEDGreen,255);    
  } else if (val<300) {
    analogWrite(LEDRed,map(val,150,300,0,255));
    analogWrite(LEDBlue,map(val,150,300,255,0)); 
    analogWrite(LEDGreen,255);
  } else if (val<450) {
    analogWrite(LEDRed,255);
    analogWrite(LEDBlue,0); 
    analogWrite(LEDGreen,255);  
  } else if (val<600) {
    analogWrite(LEDRed,255);
    analogWrite(LEDBlue,map(val,450,600,0,255)); 
    analogWrite(LEDGreen,map(val,450,600,255,0));
  } else if (val<750) {
    analogWrite(LEDRed,255);
    analogWrite(LEDBlue,255); 
    analogWrite(LEDGreen,0);  
  } else if (val<900) {
    analogWrite(LEDRed,map(val,750,900,255,0));
    analogWrite(LEDBlue,255); 
    analogWrite(LEDGreen,map(val,750,900,0,255));
  }
  delay(10);
}
