# Fritzing sketch earthquakeDetection (saved by Fritzing 0.7.0b)
breadboards: 1

parts:
  J1 = Piezo Speaker
  D1 = Zener Diode [part_number=1N4732A breakdown_voltage=5.1V package="300 mil [THT]"]
  R1 = Resistor [tolerance=±5% resistance=1M package=THT]
  Arduino1 = Arduino

nets:
  N1: J1.pin1, D1.anode, R1.Pin_0, Arduino1.GND
  N2: J1.pin2, D1.cathode, R1.Pin_1, Arduino1.A0

notes:
  Piezoelectric speakers are frequently used as beepers in watches and other electronic devices. In this project, a piezo speaker is used to detect impacts.
  earthquake detection

// code stored in the sketch: ___lockfile___.txt

