# Fritzing sketch npnPowerTransistor (saved by Fritzing 0.3.9b)
breadboards: 1

parts:
  Q1 = npn-Powertransistor [package="TO220 [THT]"]
  LED1 = Red LED - 5mm
  LED2 = Red LED - 5mm
  LED3 = Red LED - 5mm
  LED4 = Red LED - 5mm
  Arduino2 = Arduino
  R6 = Resistor [resistance=220 package=THT]
  R7 = Resistor [resistance=220 package=THT]
  R8 = Resistor [resistance=1k package=THT]
  R9 = Resistor [resistance=220 package=THT]
  R10 = Resistor [resistance=220 package=THT]

nets:
  N1: Q1.base, R8.Pin_1
  N2: Q1.collector, LED1.cathode, LED2.cathode, LED3.cathode, LED4.cathode
  N3: Q1.emitter, Arduino2.GND
  N4: LED1.anode, R9.Pin_0
  N5: LED2.anode, R10.Pin_0
  N6: LED3.anode, R6.Pin_0
  N7: LED4.anode, R7.Pin_0
  N8: Arduino2.D9, R8.Pin_0
  N9: Arduino2.+5V, R6.Pin_1, R7.Pin_1, R9.Pin_1, R10.Pin_1

notes:
  Using a power transistor with an Arduino will allow you to control outputs that need more current or higher voltages than the Arduino can provide. Related example: http://itp.nyu.edu/physcomp/Tutorials/HighCurrentLoads
