# Fritzing sketch treeduino (saved by Fritzing 0.4.3b)
breadboards: 1

parts:
  LED1 = Red LED - 5mm
  LED2 = white LED - 5mm
  LED5 = white LED - 5mm
  LED6 = Red LED - 5mm
  LED3 = white LED - 5mm
  LED4 = Red LED - 5mm
  PCB1 = Artreeno [package=THT]
  R7 = Resistor [resistance=220 package=THT]
  R8 = Resistor [resistance=220 package=THT]
  R9 = Resistor [resistance=220 package=THT]
  R10 = Resistor [resistance=220 package=THT]
  R11 = Resistor [resistance=220 package=THT]
  R12 = Resistor [resistance=220 package=THT]

nets:
  GND1: LED1.cathode, LED2.cathode, LED5.cathode, LED6.cathode, LED3.cathode, LED4.cathode, PCB1.GND1, PCB1.GND2, PCB1.GND3
  N1: LED1.anode, R11.Pin_0
  N2: LED2.anode, R12.Pin_0
  N3: LED5.anode, R8.Pin_0
  N4: LED6.anode, R10.Pin_0
  N5: LED3.anode, R9.Pin_1
  N6: LED4.anode, R7.Pin_1
  N7: PCB1.digital6, R12.Pin_1
  N8: PCB1.digital5, R7.Pin_0
  N9: PCB1.digital4, R9.Pin_0
  N10: PCB1.digital3, R10.Pin_1
  N11: PCB1.digital2, R11.Pin_1
  N12: PCB1.digital1, R8.Pin_1
