# Fritzing sketch treeduino (saved by Fritzing 0.7.0b)
breadboards: 1

parts:
  R7 = Resistor [resistance=220 tolerance=±5% package=THT]
  R8 = Resistor [resistance=220 tolerance=±5% package=THT]
  R9 = Resistor [resistance=220 tolerance=±5% package=THT]
  R10 = Resistor [resistance=220 tolerance=±5% package=THT]
  R11 = Resistor [resistance=220 tolerance=±5% package=THT]
  R12 = Resistor [resistance=220 tolerance=±5% package=THT]
  LED3 = LED - 5mm [color="White (4500K)" package="5 mm [THT]"]
  LED4 = LED - 5mm [color="Red (633nm)" package="5 mm [THT]"]
  LED6 = LED - 5mm [color="Red (633nm)" package="5 mm [THT]"]
  LED5 = LED - 5mm [color="White (4500K)" package="5 mm [THT]"]
  LED1 = LED - 5mm [color="Red (633nm)" package="5 mm [THT]"]
  LED2 = LED - 5mm [color="White (4500K)" package="5 mm [THT]"]
  PCB1 = Arduino

nets:
  N1: R7.Pin_1, LED4.anode
  N2: R8.Pin_0, LED5.anode
  N3: R9.Pin_1, LED3.anode
  N4: R10.Pin_0, LED6.anode
  N5: R11.Pin_0, LED1.anode
  N6: R12.Pin_0, LED2.anode
  N7: LED3.cathode, LED4.cathode, LED6.cathode, LED5.cathode, LED1.cathode, LED2.cathode, PCB1.GND

// code stored in the sketch: ___lockfile___.txt

